// Digital circuit ClkPulser.dig as structural Verilog
module ClkPulser (
  input  CLK,
  input  [15:0] Cnt,
  input  Trig,
  output Pulse,
  output Finished
);

  wire d_ff_as_1_q;
  wire [15:0] add_1_s;
  wire [15:1] counter_1_out;

  D_FF_AS d_ff_as_1 (.Set(1'b0), .D(1'b1), .C(Trig), .Clr(Finished), .Q(d_ff_as_1_q));  // open: nQ
  Counter #(.Bits(16)) counter_1 (
    .en(d_ff_as_1_q), .C(CLK), .clr(Finished), .out({counter_1_out, Pulse}));  // open: ovf
  Add #(.Bits(16)) add_1 (.a(Cnt), .b(Cnt), .c_i(1'b0), .s(add_1_s));  // open: c_o
  Comparator #(.Bits(16)) comparator_1 (.a({counter_1_out, Pulse}), .b(add_1_s), .eq(Finished));  // open: gt, lt

  // Notes on the sheet:
  //   CLK: Hz: 1000
  //   Cnt: default 1
endmodule
