// Digital circuit NegEdge.dig as structural Verilog
module NegEdge (
  input  i,
  output o
);

  wire delay_1_out, not_1_out;

  Delay #(.delayTime(5)) delay_1 (.in(i), .out(delay_1_out));
  nor nor_1 (o, not_1_out, i);
  not not_1 (not_1_out, delay_1_out);
endmodule
