// Digital circuit OpToTextStatic.dig as structural Verilog
module OpToTextStatic (
  input  [7:0] OP,
  output [15:0] Di0,
  output [15:0] Di1,
  output [15:0] Di2,
  output [15:0] Di3,
  output [15:0] Di4,
  output [15:0] Di5,
  output [15:0] Di6,
  output [15:0] Di7
);

  wire [7:0] rom_1_d, rom_1_d_2, rom_1_d_3, rom_1_d_4, rom_1_d_5;
  wire [63:40] rom_1_d_6;

  ROM #(.AddrBits(8), .Bits(64)) rom_1 (
    .A(OP), .sel(1'b1), .D({rom_1_d_6, rom_1_d_5, rom_1_d_4, rom_1_d_3, rom_1_d_2, rom_1_d}));
  LookUpTable #(.Bits(16)) lookuptable_1 (
    .in0(rom_1_d[0]), .in1(rom_1_d[1]), .in2(rom_1_d[2]), .in3(rom_1_d[3]), .in4(rom_1_d[4]),
    .in5(rom_1_d[5]), .in6(rom_1_d[6]), .in7(rom_1_d[7]), .out(Di7));
  LookUpTable #(.Bits(16)) lookuptable_2 (
    .in0(rom_1_d_2[0]), .in1(rom_1_d_2[1]), .in2(rom_1_d_2[2]), .in3(rom_1_d_2[3]), .in4(rom_1_d_2[4]),
    .in5(rom_1_d_2[5]), .in6(rom_1_d_2[6]), .in7(rom_1_d_2[7]), .out(Di6));
  LookUpTable #(.Bits(16)) lookuptable_3 (
    .in0(rom_1_d_3[0]), .in1(rom_1_d_3[1]), .in2(rom_1_d_3[2]), .in3(rom_1_d_3[3]), .in4(rom_1_d_3[4]),
    .in5(rom_1_d_3[5]), .in6(rom_1_d_3[6]), .in7(rom_1_d_3[7]), .out(Di5));
  LookUpTable #(.Bits(16)) lookuptable_4 (
    .in0(rom_1_d_4[0]), .in1(rom_1_d_4[1]), .in2(rom_1_d_4[2]), .in3(rom_1_d_4[3]), .in4(rom_1_d_4[4]),
    .in5(rom_1_d_4[5]), .in6(rom_1_d_4[6]), .in7(rom_1_d_4[7]), .out(Di4));
  LookUpTable #(.Bits(16)) lookuptable_5 (
    .in0(rom_1_d_5[0]), .in1(rom_1_d_5[1]), .in2(rom_1_d_5[2]), .in3(rom_1_d_5[3]), .in4(rom_1_d_5[4]),
    .in5(rom_1_d_5[5]), .in6(rom_1_d_5[6]), .in7(rom_1_d_5[7]), .out(Di3));
  LookUpTable #(.Bits(16)) lookuptable_6 (
    .in0(rom_1_d_6[40]), .in1(rom_1_d_6[41]), .in2(rom_1_d_6[42]), .in3(rom_1_d_6[43]), .in4(rom_1_d_6[44]),
    .in5(rom_1_d_6[45]), .in6(rom_1_d_6[46]), .in7(rom_1_d_6[47]), .out(Di2));
  LookUpTable #(.Bits(16)) lookuptable_7 (
    .in0(rom_1_d_6[48]), .in1(rom_1_d_6[49]), .in2(rom_1_d_6[50]), .in3(rom_1_d_6[51]), .in4(rom_1_d_6[52]),
    .in5(rom_1_d_6[53]), .in6(rom_1_d_6[54]), .in7(rom_1_d_6[55]), .out(Di1));
  LookUpTable #(.Bits(16)) lookuptable_8 (
    .in0(rom_1_d_6[56]), .in1(rom_1_d_6[57]), .in2(rom_1_d_6[58]), .in3(rom_1_d_6[59]), .in4(rom_1_d_6[60]),
    .in5(rom_1_d_6[61]), .in6(rom_1_d_6[62]), .in7(rom_1_d_6[63]), .out(Di0));

  // Notes on the sheet:
  //   contents of rom_1 (hex, n*v repeats v):
  //   4e4f502020202020,4c584920422c2320,5354415820422020,494e582042202020
  //   ,494e522042202020,4443522042202020,4d564920422c2320,524c432020202020
  //   ,4e4f502020202020,4441442042202020,4c44415820422020,4443582042202020
  //   ,494e522043202020,4443522043202020,4d564920432c2320,5252432020202020
  //   ,4e4f502020202020,4c584920442c2320,5354415820442020,494e582044202020
  //   ,494e522044202020,4443522044202020,4d564920442c2320,52414c2020202020
  //   ,4e4f502020202020,4441442044202020,4c44415820442020,4443582044202020
  //   ,494e522045202020,4443522045202020,4d564920452c2320,5241522020202020
  //   ,4e4f502020202020,4c584920482c2320,53484c4420202020,494e582048202020
  //   ,494e522048202020,4443522048202020,4d564920482c2320,4441412020202020
  //   ,4e4f502020202020,4441442048202020,4c484c4420202020,4443582048202020
  //   ,494e52204c202020,444352204c202020,4d5649204c2c2320,434d412020202020
  //   ,4e4f502020202020,4c58492053502c23,5354412020202020,494e582053502020
  //   ,494e52204d202020,444352204d202020,4d5649204d2c2320,5354432020202020
  //   ,4e4f502020202020,4441442053502020,4c44412020202020,4443582053502020
  //   ,494e522041202020,4443522041202020,4d564920412c2320,434d432020202020
  //   ,4d4f5620422c4220,4d4f5620422c4320,4d4f5620422c4420,4d4f5620422c4520
  //   ,4d4f5620422c4820,4d4f5620422c4c20,4d4f5620422c4d20,4d4f5620422c4120
  //   ,4d4f5620432c4220,4d4f5620432c4320,4d4f5620432c4420,4d4f5620432c4520
  //   ,4d4f5620432c4820,4d4f5620432c4c20,4d4f5620432c4d20,4d4f5620432c4120
  //   ,4d4f5620442c4220,4d4f5620442c4320,4d4f5620442c4420,4d4f5620442c4520
  //   ,4d4f5620442c4820,4d4f5620442c4c20,4d4f5620442c4d20,4d4f5620442c4120
  //   ,4d4f5620452c4220,4d4f5620452c4320,4d4f5620452c4420,4d4f5620452c4520
  //   ,4d4f5620452c4820,4d4f5620452c4c20,4d4f5620452c4d20,4d4f5620452c4120
  //   ,4d4f5620482c4220,4d4f5620482c4320,4d4f5620482c4420,4d4f5620482c4520
  //   ,4d4f5620482c4820,4d4f5620482c4c20,4d4f5620482c4d20,4d4f5620482c4120
  //   ,4d4f56204c2c4220,4d4f56204c2c4320,4d4f56204c2c4420,4d4f56204c2c4520
  //   ,4d4f56204c2c4820,4d4f56204c2c4c20,4d4f56204c2c4d20,4d4f56204c2c4120
  //   ,4d4f56204d2c4220,4d4f56204d2c4320,4d4f56204d2c4420,4d4f56204d2c4520
  //   ,4d4f56204d2c4820,4d4f56204d2c4c20,484c542020202020,4d4f56204d2c4120
  //   ,4d4f5620412c4220,4d4f5620412c4320,4d4f5620412c4420,4d4f5620412c4520
  //   ,4d4f5620412c4820,4d4f5620412c4c20,4d4f5620412c4d20,4d4f5620412c4120
  //   ,4144442042202020,4144442043202020,4144442044202020,4144442045202020
  //   ,4144442048202020,414444204c202020,414444204d202020,4144442041202020
  //   ,4144432042202020,4144432043202020,4144432044202020,4144432045202020
  //   ,4144432048202020,414443204c202020,414443204d202020,4144432041202020
  //   ,5355422042202020,5355422043202020,5355422044202020,5355422045202020
  //   ,5355422048202020,535542204c202020,535542204d202020,5355422041202020
  //   ,5342422042202020,5342422043202020,5342422044202020,5342422045202020
  //   ,5342422048202020,534242204c202020,534242204d202020,5342422041202020
  //   ,414e412042202020,414e412043202020,414e412044202020,414e412045202020
  //   ,414e412048202020,414e41204c202020,414e41204d202020,414e412041202020
  //   ,5852412042202020,5852412043202020,5852412044202020,5852412045202020
  //   ,5852412048202020,585241204c202020,585241204d202020,5852412041202020
  //   ,4f52412042202020,4f52412043202020,4f52412044202020,4f52412045202020
  //   ,4f52412048202020,4f5241204c202020,4f5241204d202020,4f52412041202020
  //   ,434d502042202020,434d502043202020,434d502044202020,434d502045202020
  //   ,434d502048202020,434d50204c202020,434d50204d202020,434d502041202020
  //   ,524e5a2020202020,504f502042202020,4a4e5a2020202020,4a4d502020202020
  //   ,434e5a2020202020,5055534820422020,4144492020202020,5253542030202020
  //   ,525a202020202020,5245542020202020,4a5a202020202020,4e4f502020202020
  //   ,435a202020202020,43414c4c20202020,4143492020202020,5253542031202020
  //   ,524e432020202020,504f502044202020,4a4e432020202020,4f55542020202020
  //   ,434e432020202020,5055534820442020,5355492020202020,5253542032202020
  //   ,5243202020202020,4e4f502020202020,4a43202020202020,494e202020202020
  //   ,4343202020202020,4e4f502020202020,5342492020202020,5253542033202020
  //   ,52504f2020202020,504f502048202020,4a504f2020202020,5854484c20202020
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  //   contents of lookuptable_1 (hex, n*v repeats v):
  //   90ff,100c,377,33f,38c,3bb,3fb,9003,3ff,3bf,3cf,4a3f,f3,483f,3f3
  //   ,1c3,17*0,4800,880,4b3c,4bbb,db99,2d79,1000,3000,8400,ff00,4b00
  //   ,8000,300,20,9000,90ff,100c,377,33f,38c,3bb,3fb,9003,3ff,3bf,21
  //   ,8800,3000,330,8400,4287,af7,3cf,4a3f,f3,483f,3f3,3c3,2fb,3cc
  //   ,4833,7c,31c0,f0,14cc,24cc,ff,3c7,20ff,23c7,3bb,4803,fc,90c0,a0cc
  //   ,b400,5400,9033,4812,2400,4821,1004,30,400,3cf,4a3f,f3,483f,3f3
  //   ,3c3,2fb,3cc,4833,7c,31c0,f0,14cc,24cc,ff,3c7,20ff,23c7,3bb,4803
  //   ,fc,90c0,a0cc,b400,5400,9033,4912,4800,4a21,a85,3200
  //   contents of lookuptable_2 (hex, n*v repeats v):
  //   90ff,100c,377,33f,38c,3bb,3fb,9003,3ff,3bf,3cf,4a3f,f3,483f,3f3
  //   ,1c3,17*0,4800,880,4b3c,4bbb,db99,2d79,1000,3000,8400,ff00,4b00
  //   ,8000,300,20,9000,90ff,100c,377,33f,38c,3bb,3fb,9003,3ff,3bf,21
  //   ,8800,3000,330,8400,4287,af7,3cf,4a3f,f3,483f,3f3,3c3,2fb,3cc
  //   ,4833,7c,31c0,f0,14cc,24cc,ff,3c7,20ff,23c7,3bb,4803,fc,90c0,a0cc
  //   ,b400,5400,9033,4812,2400,4821,1004,30,400,3cf,4a3f,f3,483f,3f3
  //   ,3c3,2fb,3cc,4833,7c,31c0,f0,14cc,24cc,ff,3c7,20ff,23c7,3bb,4803
  //   ,fc,90c0,a0cc,b400,5400,9033,4912,4800,4a21,a85,3200
  //   contents of lookuptable_3 (hex, n*v repeats v):
  //   90ff,100c,377,33f,38c,3bb,3fb,9003,3ff,3bf,3cf,4a3f,f3,483f,3f3
  //   ,1c3,17*0,4800,880,4b3c,4bbb,db99,2d79,1000,3000,8400,ff00,4b00
  //   ,8000,300,20,9000,90ff,100c,377,33f,38c,3bb,3fb,9003,3ff,3bf,21
  //   ,8800,3000,330,8400,4287,af7,3cf,4a3f,f3,483f,3f3,3c3,2fb,3cc
  //   ,4833,7c,31c0,f0,14cc,24cc,ff,3c7,20ff,23c7,3bb,4803,fc,90c0,a0cc
  //   ,b400,5400,9033,4812,2400,4821,1004,30,400,3cf,4a3f,f3,483f,3f3
  //   ,3c3,2fb,3cc,4833,7c,31c0,f0,14cc,24cc,ff,3c7,20ff,23c7,3bb,4803
  //   ,fc,90c0,a0cc,b400,5400,9033,4912,4800,4a21,a85,3200
  //   contents of lookuptable_4 (hex, n*v repeats v):
  //   90ff,100c,377,33f,38c,3bb,3fb,9003,3ff,3bf,3cf,4a3f,f3,483f,3f3
  //   ,1c3,17*0,4800,880,4b3c,4bbb,db99,2d79,1000,3000,8400,ff00,4b00
  //   ,8000,300,20,9000,90ff,100c,377,33f,38c,3bb,3fb,9003,3ff,3bf,21
  //   ,8800,3000,330,8400,4287,af7,3cf,4a3f,f3,483f,3f3,3c3,2fb,3cc
  //   ,4833,7c,31c0,f0,14cc,24cc,ff,3c7,20ff,23c7,3bb,4803,fc,90c0,a0cc
  //   ,b400,5400,9033,4812,2400,4821,1004,30,400,3cf,4a3f,f3,483f,3f3
  //   ,3c3,2fb,3cc,4833,7c,31c0,f0,14cc,24cc,ff,3c7,20ff,23c7,3bb,4803
  //   ,fc,90c0,a0cc,b400,5400,9033,4912,4800,4a21,a85,3200
  //   contents of lookuptable_5 (hex, n*v repeats v):
  //   90ff,100c,377,33f,38c,3bb,3fb,9003,3ff,3bf,3cf,4a3f,f3,483f,3f3
  //   ,1c3,17*0,4800,880,4b3c,4bbb,db99,2d79,1000,3000,8400,ff00,4b00
  //   ,8000,300,20,9000,90ff,100c,377,33f,38c,3bb,3fb,9003,3ff,3bf,21
  //   ,8800,3000,330,8400,4287,af7,3cf,4a3f,f3,483f,3f3,3c3,2fb,3cc
  //   ,4833,7c,31c0,f0,14cc,24cc,ff,3c7,20ff,23c7,3bb,4803,fc,90c0,a0cc
  //   ,b400,5400,9033,4812,2400,4821,1004,30,400,3cf,4a3f,f3,483f,3f3
  //   ,3c3,2fb,3cc,4833,7c,31c0,f0,14cc,24cc,ff,3c7,20ff,23c7,3bb,4803
  //   ,fc,90c0,a0cc,b400,5400,9033,4912,4800,4a21,a85,3200
  //   contents of lookuptable_6 (hex, n*v repeats v):
  //   90ff,100c,377,33f,38c,3bb,3fb,9003,3ff,3bf,3cf,4a3f,f3,483f,3f3
  //   ,1c3,17*0,4800,880,4b3c,4bbb,db99,2d79,1000,3000,8400,ff00,4b00
  //   ,8000,300,20,9000,90ff,100c,377,33f,38c,3bb,3fb,9003,3ff,3bf,21
  //   ,8800,3000,330,8400,4287,af7,3cf,4a3f,f3,483f,3f3,3c3,2fb,3cc
  //   ,4833,7c,31c0,f0,14cc,24cc,ff,3c7,20ff,23c7,3bb,4803,fc,90c0,a0cc
  //   ,b400,5400,9033,4812,2400,4821,1004,30,400,3cf,4a3f,f3,483f,3f3
  //   ,3c3,2fb,3cc,4833,7c,31c0,f0,14cc,24cc,ff,3c7,20ff,23c7,3bb,4803
  //   ,fc,90c0,a0cc,b400,5400,9033,4912,4800,4a21,a85,3200
  //   contents of lookuptable_7 (hex, n*v repeats v):
  //   90ff,100c,377,33f,38c,3bb,3fb,9003,3ff,3bf,3cf,4a3f,f3,483f,3f3
  //   ,1c3,17*0,4800,880,4b3c,4bbb,db99,2d79,1000,3000,8400,ff00,4b00
  //   ,8000,300,20,9000,90ff,100c,377,33f,38c,3bb,3fb,9003,3ff,3bf,21
  //   ,8800,3000,330,8400,4287,af7,3cf,4a3f,f3,483f,3f3,3c3,2fb,3cc
  //   ,4833,7c,31c0,f0,14cc,24cc,ff,3c7,20ff,23c7,3bb,4803,fc,90c0,a0cc
  //   ,b400,5400,9033,4812,2400,4821,1004,30,400,3cf,4a3f,f3,483f,3f3
  //   ,3c3,2fb,3cc,4833,7c,31c0,f0,14cc,24cc,ff,3c7,20ff,23c7,3bb,4803
  //   ,fc,90c0,a0cc,b400,5400,9033,4912,4800,4a21,a85,3200
  //   contents of lookuptable_8 (hex, n*v repeats v):
  //   90ff,100c,377,33f,38c,3bb,3fb,9003,3ff,3bf,3cf,4a3f,f3,483f,3f3
  //   ,1c3,17*0,4800,880,4b3c,4bbb,db99,2d79,1000,3000,8400,ff00,4b00
  //   ,8000,300,20,9000,90ff,100c,377,33f,38c,3bb,3fb,9003,3ff,3bf,21
  //   ,8800,3000,330,8400,4287,af7,3cf,4a3f,f3,483f,3f3,3c3,2fb,3cc
  //   ,4833,7c,31c0,f0,14cc,24cc,ff,3c7,20ff,23c7,3bb,4803,fc,90c0,a0cc
  //   ,b400,5400,9033,4812,2400,4821,1004,30,400,3cf,4a3f,f3,483f,3f3
  //   ,3c3,2fb,3cc,4833,7c,31c0,f0,14cc,24cc,ff,3c7,20ff,23c7,3bb,4803
  //   ,fc,90c0,a0cc,b400,5400,9033,4912,4800,4a21,a85,3200
endmodule
