// Digital circuit main.dig as structural Verilog
module main (
  input  clk
);

  wire _16bitAddrLoad_Call, _16bitAddrLoad_Jmp, _16bitAddrLoad_Lda, _16bitAddrLoad_Lhld, _16bitAddrLoad_Lxi,
       _7474_1_pin1, _7474_1_pin6, _74112_1_pin3, _74112_1_pin6, _74112_1_pin9, _74153_1_pin7, _74157_1_pin4,
       _74157_1_pin12, _74163_1_pin2, _74163_1_pin12, _74163_1_pin13, _74163_1_pin14, _74175_1_pin2,
       _74175_1_pin7, _74175_1_pin9, _74175_1_pin10, _74193_1_pin12, _74193_1_pin13, _74193_2_pin12,
       _74193_2_pin13, _74193_3_pin12, _74193_3_pin13, _74193_5_pin12, _74193_5_pin13, _74193_6_pin12,
       _74193_6_pin13, _74193_7_pin12, _74193_7_pin13, _74238_1_pin7, _74238_1_pin10, _74238_1_pin11,
       _74238_2_pin7, _74238_2_pin9, _74238_2_pin10, _74238_2_pin11, _74238_2_pin12, _74238_2_pin13,
       _74238_2_pin14, _74238_2_pin15, _74238_3_pin7, _74238_3_pin9, _74238_3_pin10, _74238_3_pin11,
       _74238_3_pin12, _74238_3_pin13, _74238_3_pin14, _74238_3_pin15, _74238_4_pin7, _74238_4_pin10,
       _74238_4_pin11, _74238_4_pin12, _74238_4_pin13, _74238_4_pin14, _74238_4_pin15, _74238_14_pin14,
       _74283_1_p5, _74283_3_p5, _74283_5_p4, _74283_6_p4, _74541_1_pin2, _74541_1_pin3, _74541_1_pin4,
       _74541_1_pin5, _74541_1_pin6, _74541_1_pin7, _74541_1_pin8, _74541_1_pin9, _74541_17_pin11,
       _74541_18_pin18, _74541_21_pin3, _74541_21_pin7, A0, A1, A2, A3, A4, A5, A6, A7, A8, A9, A10, A11,
       A12, A13, A14, A15, Abus2Rbus_E, Ac_ALU, Ack_IO, ACo, ADC, ADD, ALUck_ALU, ALUck_Daa, ALUck_InrDcr,
       ALUe_ALU, ALUe_Daa, ALUe_InrDcr, ANA, and_3_out, and_8_out, and_16_out, and_24_out, and_25_out,
       and_29_out, and_31_out, and_32_out, and_36_out, and_52_out, and_53_out, and_54_out, and_57_out,
       and_60_out, and_61_out, and_62_out, and_68_out, and_69_out, and_72_out, and_78_out, and_80_out,
       and_83_out, and_90_out, and_92_out, and_93_out, and_98_out, and_99_out, and_100_out, and_101_out,
       and_103_out, and_107_out, and_109_out, and_111_out, and_112_out, and_113_out, and_115_out,
       and_116_out, and_117_out, and_118_out, and_119_out, and_120_out, and_121_out, and_126_out,
       and_127_out, and_128_out, and_129_out, and_130_out, and_131_out, and_132_out, and_133_out,
       and_140_out, and_141_out, and_142_out, and_143_out, and_144_out, and_145_out, and_146_out,
       and_147_out, and_154_out, and_155_out, and_156_out, and_163_out, and_164_out, and_165_out,
       and_168_out, and_169_out, and_170_out, and_171_out, and_172_out, and_179_out, and_180_out,
       and_186_out, and_191_out, and_192_out, and_193_out, and_194_out, and_195_out, and_215_out,
       and_223_out, and_227_out, AuxCarryFlag, B_Ck, BC_E_Dad, BC_E_Inx, BC_E_Ldax, BC_E_Xchg, BCck_Lxi,
       C_Ck, CarryCk_Daa, CarryCk_Dad, CarryCk_Rot, CarryCk_Stc, CarryData_Dad, CarryData_Rot, CarryData_Stc,
       CarryFlag, CarryRegInc, clkpulser_1_pulse, ClrInt, CMP, Cy_ALU, CYo, D0, D1, D2, D3, D4, D5, D6, D7,
       D_Ck, Db00E_Rst, DBIN, DBIN_ALU, DBIN_Fetch16, DBIN_FetchOp, DBIN_InOut, DBIN_Lda, DBIN_Ldax,
       DBIN_Lhld, DBIN_Mov, DBIN_Mvi, DBIN_Pop, DBIN_Ret, DBIN_Xthl, DbIR345E_Rst, DE_E_Dad, DE_E_Inx,
       DE_E_Ldax, DE_E_Xchg, DEck_Lxi, DEck_Xchg, delay_1_out, delay_2_out, delay_3_out,
       DisconnectRegFile_ALU, DisconnectRegFile_Call, DisconnectRegFile_Daa, DisconnectRegFile_Dad,
       DisconnectRegFile_Inr, DisconnectRegFile_Inx, DisconnectRegFile_Jmp, DisconnectRegFile_Ldax,
       DisconnectRegFile_Lhld, DisconnectRegFile_Lxi, DisconnectRegFile_Mov, DisconnectRegFile_Mvi,
       DisconnectRegFile_Out, DisconnectRegFile_Push, DisconnectRegFile_Ret, DisconnectRegFile_Rst,
       DisconnectRegFile_SphlPchl, DisconnectRegFile_Xchg, DisconnectRegFile_Xthl, DisconnectRegFileHigh,
       DisconnectRegFileHigh_Fetch16, DisconnectRegFileHigh_Ldhl, DisconnectRegFileHigh_Mov,
       DisconnectRegFileLow, DisconnectRegFileLow_Fetch16, DisconnectRegFileLow_Ldhl,
       DisconnectRegFileLow_Mov, driver_1_out, DstA_LDA, DstA_Ldax, DstA_PopPsw, DstE_InrDcr, DstE_InxDcx,
       DstE_MOV, DstE_MVI, DstE_POP, DstH_LDHL, DstH_Xtld, DstIsMem, DstL_Dad, DstL_LDHL, DstL_Xtld, DstM,
       E_Ck, enaALU_ALU, enableCarryIn, Finish_ALU, Finish_Call, Finish_Di, Finish_Hlt, Finish_Inx,
       Finish_IO, Finish_Jmp, Finish_Lda, Finish_Ldax, Finish_LDHL, Finish_Lxi, Finish_Mov, Finish_Mvi,
       Finish_Nop, Finish_Pop, Finish_Push, Finish_Ret, Finish_Rst, Finish_SphlPchl, Finish_XCHG,
       Finish_Xthl, flagCondMet, Flags2DB, FlgUpdateCk_PopPsw, FlgUpdateE_PopPsw, GrpALU, GrpBranchControl,
       GrpCondCall, GrpCondJmp, GrpCondRet, GrpDatatransfer, GrpDcr, GrpImmOp, GrpInr, GrpInrDcr, GrpInxDcx,
       GrpJmpOthers, GrpLoadStore, GrpLxiDad, GrpMOV, GrpMVI, GrpPOP, GrpPUSH, GrpRotFlag, GrpRST,
       GrpStackPop, GrpStackPsh, H_Ck, HL_E_ALU, HL_E_Dad, HL_E_Inx, HL_E_Xchg, HL_E_Xthl, HLck_Lxi, HLDA,
       HlE_Mov, HLTA, HOLD, HoldDB2AB_Ck, HoldDB2AB_E, I_out, IncHigh2DbusE, IncHigh2DbusE_Dad,
       IncHigh2DbusE_Inx, IncHigh2DbusE_Xthl, IncLow2DbusE, IncLow2DbusE_Dad, IncLow2DbusE_Inx,
       IncLow2DbusE_Xthl, INP, INT, INTA, INTE, IntFlag, IO_0, IO_1, IO_2, IO_3, IO_4, IO_5, IO_6, IO_7,
       IO_8, IO_9, IO_10, IO_11, IO_12, IO_13, IO_14, IO_15, IOR_InOut, IOW_InOut, IrLatch_FetchOp, isArith,
       isSubtraction, KillSrc_Mov, L_Ck, LowInrDcr, LowPOP, LowPUSH, M1, MemE_Rst, MEMR, MEMR_InOut,
       MEMR_Mvi, MEMW_Call, MEMW_Lda, MEMW_Ldax, MEMW_Ldhl, MEMW_Mov, MEMW_Mvi, MEMW_Push, MEMW_Rst,
       MEMW_Xthl, nand_1_out, negedge_1_o, negedge_2_o, nflagCondMet, nIOR, nIOW, nIR0, nIR3, nMEMR, nMEMW,
       nor_17_out, nor_18_out, nor_19_out, nor_20_out, nor_21_out, nor_22_out, nor_23_out, nor_25_out,
       nor_26_out, nor_27_out, nor_28_out, nor_30_out, nor_31_out, nor_32_out, nor_33_out, nor_34_out,
       not_1_out, not_2_out, not_3_out, not_4_out, not_7_out, not_8_out, not_9_out, not_11_out, not_12_out,
       not_13_out, not_14_out, not_15_out, not_16_out, not_17_out, not_18_out, not_19_out, not_20_out,
       not_21_out, not_22_out, not_23_out, not_24_out, not_25_out, not_26_out, not_27_out, not_28_out,
       not_32_out, not_33_out, not_34_out, not_35_out, not_36_out, not_37_out, not_38_out, not_39_out,
       not_41_out, not_42_out, not_43_out, not_44_out, not_45_out, not_46_out, not_49_out, not_50_out,
       not_51_out, not_52_out, not_53_out, not_54_out, not_55_out, not_56_out, nWO, nWR, OpCall, OpCMA,
       OpCMC, OpDAA, OpDAD, OpDi, OpEi, OpHLT, OpIn, OpJMP, OpLDA, OpLdaxBC, OpLdaxDE, OpLHLD, OpNOP, OpOut,
       OpPCHL, OpRAL, OpRAR, OpRet, OpRLC, OpRRC, OpSHLD, OpSPHL, OpSTA, OpStaxBC, OpStaxDE, OpSTC, OpXcHG,
       OpXtHL, or_3_out, or_4_out, or_5_out, or_6_out, or_7_out, or_8_out, or_12_out, or_16_out, or_18_out,
       or_19_out, or_20_out, or_23_out, or_29_out, or_37_out, or_38_out, or_39_out, or_40_out, or_41_out,
       or_46_out, or_47_out, or_48_out, or_49_out, or_59_out, or_60_out, or_61_out, or_64_out, or_65_out,
       or_70_out, or_72_out, or_75_out, or_76_out, or_77_out, or_80_out, or_81_out, or_82_out, or_83_out,
       or_84_out, or_85_out, or_86_out, or_87_out, or_88_out, or_89_out, or_97_out, or_98_out, or_100_out,
       or_111_out, or_112_out, or_113_out, or_114_out, or_115_out, or_116_out, or_117_out, or_118_out,
       or_119_out, or_120_out, or_121_out, or_126_out, or_129_out, or_132_out, or_134_out, or_135_out,
       or_136_out, or_137_out, or_138_out, or_139_out, or_140_out, or_141_out, or_142_out, or_143_out,
       or_145_out, or_146_out, or_147_out, or_149_out, or_155_out, ORA, OUT, P0, P0x, P1, P2, P3, P4, P5,
       ParityFlag, PcDbHighE_Call, PcDbHighE_Rst, PcDbLowE_Call, PcDbLowE_Rst, PcE_ALU, PcInc_ALU,
       PcInc_Fetch16, PcInc_FetchOp, PcLoadCk_Call1, PcLoadCk_Jmp, PcLoadCk_Ret1, PcLoadCk_SphlPchl, Ph1,
       Ph2, Po_ALU, pulldown_1_out, pulldown_3_out, pulldown_5_out, R_out, READY, RegA_Ck, RegA_E,
       RegAck_ALU, RegB_Ck, RegB_E, RegC_Ck, RegC_E, RegD_Ck, RegD_E, RegE_Ck, RegE_E, RegFileAdd00orFF,
       RegFileAddHL, RegH_Ck, RegH_E, RegHigh2DB_Dir, RegHigh2DbusE, RegHigh2DbusE_ALU, RegHigh2DbusE_Inr,
       RegHigh2DbusE_Ldhl, RegHigh2DbusE_Mov, RegHigh2DbusE_Push, RegIncCarry, RegL_Ck, RegL_E,
       RegLow2DB_Dir, RegLow2DbusE, RegLow2DbusE_ALU, RegLow2DbusE_Lda, RegLow2DbusE_Ldax, RegLow2DbusE_Ldhl,
       RegLow2DbusE_Mov, RegLow2DbusE_Push, Regs2AbusE, Regs2AbusE_Inx, Regs2AbusE_Lda, Regs2AbusE_Ldax,
       Regs2AbusE_Lhld, Regs2AbusE_Mov, Regs2AbusLat, Regs2AbusLat_Dad, Regs2AbusLat_Fetch16,
       Regs2AbusLat_Inx, Regs2AbusLat_Ldax, Regs2AbusLat_Lhld, Regs2AbusLat_Mov, Regs2AbusLat_Xthl, RegW_Ck,
       RegW_E, RegWck_Ret, RegWck_Rst, RegZ_Ck, RegZ_E, RegZck_Fetch16, RegZck_Ret, RegZck_Rst, RESET,
       reset_1_out, reset_2_out, reset_3_out, reset_4_out, reset_5_out, RP_BC, RP_DE, RP_HL, RP_SP,
       rs_ff_as_1_q, rs_ff_as_2_q, S_out, SBB, SetInt, SignFlag, So_ALU, SpDec_Call, SpDec_Inx, SpE_Xthl,
       SpInc_Inx, SpInc_Pop, SpInc_Xthl, SpIncCk_Ret, SpLoadCk_Lxi, SpLoadCk_SphlPchl, SrcA, SrcA_PushPsw,
       SrcB, SrcC, SrcD, SrcE, SrcH, SrcL, SrcM, STACK, SUB, SYNC, T0, T1, T2, T3, T4, T5, T_out,
       telnet_1_av, TICK, Toff, W_Ck, WAIT, WR, WZ_E_Xchg, WZck_Xchg, xor_1_out, xor_10_out, xor_11_out,
       xor_12_out, xor_13_out, xor_14_out, xor_15_out, xor_16_out, xor_17_out, xor_18_out, xor_19_out,
       xor_20_out, xor_21_out, xor_22_out, xor_23_out, xor_24_out, xor_25_out, xor_26_out, XRA, Z_Ck,
       ZeroFlag, Zo_ALU, ZW_plus_1, ZW_plus_1_Inx, ZW_plus_1_LDHL;
  wire [2:0] DSTREG;
  wire [3:0] multiplexer_1_out, multiplexer_1_out_2, multiplexer_2_out, multiplexer_2_out_2;
  wire [5:1] _74574_13_pin13;
  wire [7:0] _74541_19_pin11, _74574_1_pin12, AccBus, AluResultBus, DataBus, IR, RAM1_d, RegB, RegC, RegD,
       RegE, RegH, RegHighBus, RegL, RegLowBus, RegW, RegZ, telnet_1_out, undriven_9, undriven_10,
       undriven_11, undriven_12, undriven_13, xor_9_out;
  wire [15:0] PC, SP, undriven, undriven_2, undriven_3, undriven_4, undriven_5, undriven_6, undriven_7,
       undriven_8;

  not not_1 (not_1_out, IR[0]);
  not not_2 (not_2_out, DSTREG[0]);
  not not_3 (not_3_out, IR[7]);
  LED led_1 (.in(OpXtHL));
  and and_1 (HL_E_Xthl, OpXtHL, T1);
  and and_2 (Regs2AbusLat_Xthl, OpXtHL, P1);
  and and_3 (and_3_out, OpXtHL, T2);
  and and_4 (DstL_Xtld, OpXtHL, P2);
  and and_5 (SpInc_Xthl, OpXtHL, T3);
  and and_6 (DstH_Xtld, OpXtHL, P3);
  and and_7 (IncHigh2DbusE_Xthl, OpXtHL, T4);
  and and_8 (and_8_out, OpXtHL, P4);
  and and_9 (IncLow2DbusE_Xthl, OpXtHL, T5);
  and and_10 (Finish_Xthl, OpXtHL, P5);
  nand nand_1 (nand_1_out, not_1_out, IR[1], IR[2], not_2_out, DSTREG[1], DSTREG[2], IR[6], not_3_out);
  or or_1 (DBIN_Xthl, and_3_out, SpInc_Xthl);
  or or_2 (MEMW_Xthl, and_8_out, Finish_Xthl);
  or or_3 (or_3_out, OpLdaxBC, OpLdaxDE);
  or or_4 (or_4_out, OpStaxBC, OpStaxDE);
  or or_5 (or_5_out, OpLdaxBC, OpStaxBC);
  or or_6 (or_6_out, OpLdaxDE, OpStaxDE);
  not not_4 (not_4_out, nand_1_out);
  or or_7 (or_7_out, nWR, IO_1);
  or or_8 (or_8_out, or_3_out, or_4_out);
  LED led_2 (.in(OpNOP));
  and and_11 (Finish_Nop, OpNOP, T1);
  // Probe on not_4_out
  LED HLT (.in(not_4_out));
  and and_12 (OpHLT, not_4_out, T1);
  and and_13 (Finish_Hlt, not_4_out, P1);
  or or_9 (DisconnectRegFile_Xthl, HL_E_Xthl, IncHigh2DbusE_Xthl, IncLow2DbusE_Xthl);
  or or_10 (SpE_Xthl, DBIN_Xthl, IncHigh2DbusE_Xthl, IncLow2DbusE_Xthl);
  LED led_3 (.in(or_8_out));
  Seven_Seg_Hex seven_seg_hex_1 (.d(_74574_1_pin12[7:4]), .dp(1'b0));
  _74574 _74574_1 (
    .pin1(1'b0), .pin2(D0), .pin3(D1), .pin4(D2), .pin5(D3), .pin6(D4), .pin7(D5), .pin8(D6), .pin9(D7),
    .pin10(1'b0), .pin11(or_7_out), .pin12(_74574_1_pin12[7]), .pin13(_74574_1_pin12[6]),
    .pin14(_74574_1_pin12[5]), .pin15(_74574_1_pin12[4]), .pin16(_74574_1_pin12[3]),
    .pin17(_74574_1_pin12[2]), .pin18(_74574_1_pin12[1]), .pin19(_74574_1_pin12[0]), .pin20(1'b1));
  and and_14 (BC_E_Ldax, or_5_out, T1);
  and and_15 (DE_E_Ldax, or_6_out, T1);
  and and_16 (and_16_out, or_8_out, T1);
  and and_17 (Regs2AbusLat_Ldax, or_8_out, P1);
  and and_18 (Regs2AbusE_Ldax, or_8_out, T2);
  and and_19 (Finish_Ldax, or_8_out, P2);
  and and_20 (DBIN_Ldax, or_3_out, T2);
  and and_21 (DstA_Ldax, or_3_out, P2);
  and and_22 (RegLow2DbusE_Ldax, or_4_out, T2);
  and and_23 (MEMW_Ldax, or_4_out, P2);
  Seven_Seg_Hex seven_seg_hex_2 (.d(_74574_1_pin12[3:0]), .dp(1'b0));
  or or_11 (DisconnectRegFile_Ldax, RegLow2DbusE_Ldax, and_16_out);
  LED led_4 (.in(OpEi));
  and and_24 (and_24_out, OpEi, T1);
  LED led_5 (.in(OpDi));
  and and_25 (and_25_out, OpDi, T1);
  or or_12 (or_12_out, nIOR, IO_15);
  _74138 _74138_1 (
    .pin1(A0), .pin2(A1), .pin3(A2), .pin4(1'b0), .pin5(A3), .pin6(1'b1), .pin7(IO_7), .pin8(1'b0),
    .pin9(IO_6), .pin10(IO_5), .pin11(IO_4), .pin12(IO_3), .pin13(IO_2), .pin14(IO_1), .pin15(IO_0),
    .pin16(1'b1));
  _74138 _74138_2 (
    .pin1(A0), .pin2(A1), .pin3(A2), .pin4(1'b0), .pin5(1'b0), .pin6(A3), .pin7(IO_15), .pin8(1'b0),
    .pin9(IO_14), .pin10(IO_13), .pin11(IO_12), .pin12(IO_11), .pin13(IO_10), .pin14(IO_9), .pin15(IO_8),
    .pin16(1'b1));
  not not_5 (ClrInt, and_25_out);
  _74541 _74541_1 (
    .pin1(or_12_out), .pin2(_74541_1_pin2), .pin3(_74541_1_pin3), .pin4(_74541_1_pin4), .pin5(_74541_1_pin5),
    .pin6(_74541_1_pin6), .pin7(_74541_1_pin7), .pin8(_74541_1_pin8), .pin9(_74541_1_pin9), .pin10(1'b0),
    .pin11(D7), .pin12(D6), .pin13(D5), .pin14(D4), .pin15(D3), .pin16(D2), .pin17(D1), .pin18(D0),
    .pin19(or_12_out), .pin20(1'b1));
  DipSwitch dipswitch_1 (.out(_74541_1_pin2));
  DipSwitch dipswitch_2 (.out(_74541_1_pin3));
  DipSwitch dipswitch_3 (.out(_74541_1_pin4));
  DipSwitch dipswitch_4 (.out(_74541_1_pin5));
  DipSwitch dipswitch_5 (.out(_74541_1_pin6));
  DipSwitch dipswitch_6 (.out(_74541_1_pin7));
  DipSwitch dipswitch_7 (.out(_74541_1_pin8));
  DipSwitch dipswitch_8 (.out(_74541_1_pin9));
  PullDown pulldown_1 (.out(pulldown_1_out));
  _74175 _74175_1 (
    .pin1(SetInt), .pin2(_74175_1_pin2), .pin4(and_24_out), .pin5(_74175_1_pin2), .pin7(_74175_1_pin7),
    .pin8(1'b0), .pin9(_74175_1_pin9), .pin10(_74175_1_pin10), .pin11(SetInt), .pin12(_74175_1_pin7),
    .pin13(_74175_1_pin10), .pin16(1'b1));  // open: pin3, pin6, pin14, pin15
  or or_13 (_74175_1_pin9, and_24_out, T0);
  or or_14 (Finish_Di, and_24_out, and_25_out);
  LED u_Tick (.in(TICK));
  // ScopeTrigger #(.maxStepCount(10000)) scopetrigger_1: pin names not known; wires that end beside it: TICK, pulldown_1_out, pulldown_1_out
  LED led_6 (.in(GrpInxDcx));
  and and_26 (DisconnectRegFile_Inx, GrpInxDcx, T1);
  and and_27 (Regs2AbusLat_Inx, GrpInxDcx, P1);
  and and_28 (IncLow2DbusE_Inx, GrpInxDcx, T2);
  and and_29 (and_29_out, GrpInxDcx, P2);
  and and_30 (IncHigh2DbusE_Inx, GrpInxDcx, T3);
  and and_31 (and_31_out, GrpInxDcx, P3);
  not not_6 (RegHigh2DB_Dir, RegHigh2DbusE);
  and and_32 (and_32_out, DisconnectRegFileHigh, RegHigh2DbusE);
  and and_33 (HL_E_Inx, RP_HL, DisconnectRegFile_Inx);
  and and_34 (DE_E_Inx, RP_DE, DisconnectRegFile_Inx);
  and and_35 (BC_E_Inx, RP_BC, DisconnectRegFile_Inx);
  and and_36 (and_36_out, nIOR, nIOW);
  LED u_OpIn (.in(OpIn));
  LED u_OpOut (.in(OpOut));
  or or_15 (Regs2AbusE_Inx, DisconnectRegFile_Inx, IncLow2DbusE_Inx, IncHigh2DbusE_Inx);
  or or_16 (or_16_out, IncLow2DbusE_Inx, IncHigh2DbusE_Inx);
  or or_17 (DstE_InxDcx, and_29_out, and_31_out);
  not not_7 (not_7_out, Abus2Rbus_E);
  // _74245 _74245_1: pin names not known; wires that end beside it: 1'b1, RegHigh2DB_Dir, and_32_out, 1'b0
  // _74574 _74574_2: pin names not known; wires that end beside it: 1'b1, 1'b0
  // _74574 _74574_3: pin names not known; wires that end beside it: 1'b1, 1'b0
  // _74574 _74574_4: pin names not known; wires that end beside it: 1'b1, 1'b0
  // _74574 _74574_5: pin names not known; wires that end beside it: 1'b1, 1'b0
  // Probe on TICK
  BusSplitter #(.Bits(8)) bussplitter_1 (.D(DataBus), .OE(not_8_out));  // open: D0, D1, D2, D3, D4, D5, D6, D7
  BusSplitter #(.Bits(8)) bussplitter_2 (.D(RegHighBus), .OE(RegHigh2DB_Dir));  // open: D0, D1, D2, D3, D4, D5, D6, D7
  or or_18 (or_18_out, nIOR, IO_1);
  or or_19 (or_19_out, and_36_out, IO_1);
  or or_20 (or_20_out, nIOR, IO_0);
  and and_37 (SpDec_Inx, DSTREG[0], RP_SP, DisconnectRegFile_Inx);
  and and_38 (SpInc_Inx, RP_SP, DisconnectRegFile_Inx, nIR3);
  and and_39 (RegFileAdd00orFF, DSTREG[0], or_16_out);
  and and_40 (ZW_plus_1_Inx, or_16_out, nIR3);
  not not_8 (not_8_out, RegHigh2DB_Dir);
  // Probe on or_19_out
  // Probe on or_20_out
  or or_21 (Finish_Inx, SpDec_Inx, SpInc_Inx, and_31_out);
  Telnet telnet_1 (
    .in({D7, D6, D5, D4, D3, D2, D1, D0}), .C(or_19_out), .wr(OpOut), .rd(OpIn), .out(telnet_1_out),
    .av(telnet_1_av));
  _74541 _74541_2 (
    .pin1(or_20_out), .pin2(telnet_1_av), .pin3(1'b1), .pin4(1'b0), .pin5(1'b0), .pin6(1'b0), .pin7(1'b0),
    .pin8(1'b0), .pin9(1'b0), .pin10(1'b0), .pin11(D7), .pin12(D6), .pin13(D5), .pin14(D4), .pin15(D3),
    .pin16(D2), .pin17(D1), .pin18(D0), .pin19(or_20_out), .pin20(1'b1));
  // _74541 _74541_3: pin names not known; wires that end beside it: RegB_Ck, 1'b0, 1'b1, RegB_E, RegB_E, 1'b0
  // _74541 _74541_4: pin names not known; wires that end beside it: RegD_Ck, 1'b0, 1'b1, RegD_E, RegD_E, 1'b0
  // _74541 _74541_5: pin names not known; wires that end beside it: RegH_Ck, 1'b0, 1'b1, RegH_E, RegH_E, 1'b0
  // _74541 _74541_6: pin names not known; wires that end beside it: RegW_Ck, 1'b0, 1'b1, RegW_E, RegW_E, 1'b0
  // Probe on telnet_1_out
  LED led_7 (.in(OpDAD));
  and and_41 (DisconnectRegFile_Dad, OpDAD, T1);
  and and_42 (Regs2AbusLat_Dad, OpDAD, P1);
  and and_43 (IncHigh2DbusE_Dad, OpDAD, T2);
  and and_44 (CarryCk_Dad, OpDAD, P2);
  and and_45 (IncLow2DbusE_Dad, OpDAD, T3);
  and and_46 (DstL_Dad, OpDAD, P3);
  // Probe on or_18_out
  and and_47 (Abus2Rbus_E, RP_SP, DisconnectRegFile_Dad);
  and and_48 (HL_E_Dad, RP_HL, DisconnectRegFile_Dad);
  and and_49 (DE_E_Dad, RP_DE, DisconnectRegFile_Dad);
  and and_50 (BC_E_Dad, RP_BC, DisconnectRegFile_Dad);
  or or_22 (RegFileAddHL, IncHigh2DbusE_Dad, IncLow2DbusE_Dad);
  and and_51 (CarryData_Dad, IncHigh2DbusE_Dad, CarryRegInc);
  _74541 _74541_7 (
    .pin1(or_18_out), .pin2(telnet_1_out[0]), .pin3(telnet_1_out[1]), .pin4(telnet_1_out[2]),
    .pin5(telnet_1_out[3]), .pin6(telnet_1_out[4]), .pin7(telnet_1_out[5]), .pin8(telnet_1_out[6]),
    .pin9(telnet_1_out[7]), .pin10(1'b0), .pin11(D7), .pin12(D6), .pin13(D5), .pin14(D4), .pin15(D3),
    .pin16(D2), .pin17(D1), .pin18(D0), .pin19(or_18_out), .pin20(1'b1));
  LED led_8 (.in(GrpMOV));
  and and_52 (and_52_out, DstIsMem, GrpMOV);
  and and_53 (and_53_out, GrpMOV, SrcM);
  // _74541 _74541_8: pin names not known; wires that end beside it: 1'b0, not_7_out, not_7_out, 1'b1
  or or_23 (or_23_out, and_52_out, and_53_out);
  and and_54 (and_54_out, T2, and_52_out);
  and and_55 (MEMW_Mov, and_52_out, P2);
  and and_56 (DBIN_Mov, T2, and_53_out);
  and and_57 (and_57_out, and_53_out, P2);
  Seven_Seg_Hex seven_seg_hex_3 (.d(RegB[7:4]), .dp(1'b0));
  Seven_Seg_Hex seven_seg_hex_4 (.d(RegD[7:4]), .dp(1'b0));
  Seven_Seg_Hex seven_seg_hex_5 (.d(RegH[7:4]), .dp(1'b0));
  Seven_Seg_Hex seven_seg_hex_6 (.d(RegW[7:4]), .dp(1'b0));
  not not_9 (not_9_out, or_23_out);
  and and_58 (HlE_Mov, T1, or_23_out);
  and and_59 (Regs2AbusLat_Mov, or_23_out, P1);
  and and_60 (and_60_out, nIR0, and_54_out);
  and and_61 (and_61_out, and_54_out, IR[0]);
  Seven_Seg_Hex seven_seg_hex_7 (.d(RegHighBus[7:4]), .dp(1'b0));
  Seven_Seg_Hex seven_seg_hex_8 (.d(RegB[3:0]), .dp(1'b0));
  Seven_Seg_Hex seven_seg_hex_9 (.d(RegD[3:0]), .dp(1'b0));
  Seven_Seg_Hex seven_seg_hex_10 (.d(RegH[3:0]), .dp(1'b0));
  Seven_Seg_Hex seven_seg_hex_11 (.d(RegW[3:0]), .dp(1'b0));
  or or_24 (Regs2AbusE_Mov, and_54_out, DBIN_Mov);
  Seven_Seg_Hex seven_seg_hex_12 (.d(RegHighBus[3:0]), .dp(1'b0));
  and and_62 (and_62_out, GrpMOV, not_9_out, P1);
  and and_63 (KillSrc_Mov, HlE_Mov, and_52_out);
  or or_25 (DisconnectRegFile_Mov, HlE_Mov, and_54_out);
  or or_26 (_16bitAddrLoad_Call, OpCall, GrpCondCall);
  and and_64 (DisconnectRegFileHigh_Mov, not_9_out, GrpMOV, T1, nIR0);
  and and_65 (DisconnectRegFileLow_Mov, not_9_out, GrpMOV, T1, IR[0]);
  LED led_9 (.in(_16bitAddrLoad_Call));
  and and_66 (PcDbHighE_Call, _16bitAddrLoad_Call, T3);
  and and_67 (PcDbLowE_Call, _16bitAddrLoad_Call, T4);
  and and_68 (and_68_out, _16bitAddrLoad_Call, P3);
  and and_69 (and_69_out, _16bitAddrLoad_Call, P4);
  and and_70 (DisconnectRegFile_Call, _16bitAddrLoad_Call, T5);
  and and_71 (PcLoadCk_Call1, _16bitAddrLoad_Call, P5);
  and and_72 (and_72_out, GrpCondCall, P2, nflagCondMet);
  or or_27 (RegHigh2DbusE_Mov, DisconnectRegFileHigh_Mov, and_60_out);
  or or_28 (RegLow2DbusE_Mov, DisconnectRegFileLow_Mov, and_61_out);
  or or_29 (or_29_out, Regs2AbusE, DisconnectRegFile_Xthl);
  or or_30 (SpDec_Call, PcDbHighE_Call, PcDbLowE_Call);
  or or_31 (MEMW_Call, and_68_out, and_69_out);
  or or_32 (Finish_Call, PcLoadCk_Call1, and_72_out);
  or or_33 (DstE_MOV, and_57_out, and_62_out);
  or or_34 (Finish_Mov, and_57_out, MEMW_Mov, and_62_out);
  Multiplexer #(.Selector_Bits(2), .Bits(8)) multiplexer_1 (
    .sel({RegFileAddHL, RegFileAdd00orFF}), .in_0({8{1'b0}}), .in_1({8{1'b1}}), .in_2(RegH), .in_3(RegH),
    .out({multiplexer_1_out_2, multiplexer_1_out}));
  LED led_10 (.in(GrpRST));
  and and_73 (DbIR345E_Rst, GrpRST, T1);
  and and_74 (RegZck_Rst, GrpRST, P1);
  and and_75 (Db00E_Rst, GrpRST, T2);
  and and_76 (RegWck_Rst, GrpRST, P2);
  and and_77 (PcDbHighE_Rst, GrpRST, T3);
  and and_78 (and_78_out, GrpRST, P3);
  and and_79 (PcDbLowE_Rst, GrpRST, T4);
  and and_80 (and_80_out, GrpRST, P4);
  and and_81 (DisconnectRegFile_Rst, GrpRST, T5);
  and and_82 (Finish_Rst, GrpRST, P5);
  or or_35 (MemE_Rst, PcDbHighE_Rst, PcDbLowE_Rst);
  or or_36 (MEMW_Rst, and_78_out, and_80_out);
  or or_37 (or_37_out, DisconnectRegFile_Out, DisconnectRegFile_Inx, DisconnectRegFile_Jmp, DisconnectRegFile_Mvi, DisconnectRegFile_Lxi, DisconnectRegFile_Push, DisconnectRegFile_Call, DisconnectRegFile_Ret, DisconnectRegFile_Xchg, DisconnectRegFile_Rst, DisconnectRegFile_SphlPchl, DisconnectRegFile_Mov, DisconnectRegFile_Lhld, DisconnectRegFile_Ldax, DisconnectRegFile_Xthl, DisconnectRegFile_Dad, DisconnectRegFile_ALU, DisconnectRegFile_Inr, DisconnectRegFile_Daa);
  // _74283 _74283_1: pin names not known; wires that end beside it: Regs2AbusLat, RegIncCarry, 1'b1, 1'b0, _74283_1_p5
  // _74541 _74541_9: pin names not known; wires that end beside it: 1'b0, or_29_out, or_29_out, 1'b1
  // _74541 _74541_10: pin names not known; wires that end beside it: 1'b0, IncHigh2DbusE, IncHigh2DbusE, 1'b1
  // _74283 _74283_2: pin names not known; wires that end beside it: _74283_1_p5, 1'b1, 1'b0, CarryRegInc
  PullDown pulldown_2 (.out(BC_E_Xchg));
  or or_38 (or_38_out, BC_E_Xchg, BC_E_Ldax, BC_E_Inx, BC_E_Dad, BC_E_Dad);
  or or_39 (or_39_out, DE_E_Dad, DE_E_Xchg, DE_E_Ldax, DE_E_Inx, DE_E_Inx);
  or or_40 (or_40_out, HL_E_ALU, HL_E_Inx, HlE_Mov, DisconnectRegFile_Mvi, DisconnectRegFile_SphlPchl, HL_E_Xchg, HL_E_Xthl, HL_E_Dad, HL_E_Dad);
  or or_41 (or_41_out, DisconnectRegFile_Call, DisconnectRegFile_Call, DisconnectRegFile_Ret, DisconnectRegFile_Rst, DisconnectRegFile_Jmp, DisconnectRegFile_Lxi, DisconnectRegFile_Lhld, WZ_E_Xchg, WZ_E_Xchg);
  or or_42 (Z_Ck, RegZck_Fetch16, RegZck_Rst, RegZck_Ret);
  or or_43 (W_Ck, Regs2AbusLat_Fetch16, RegWck_Rst, RegWck_Ret);
  or or_44 (DisconnectRegFileHigh, DisconnectRegFileHigh_Ldhl, DisconnectRegFileHigh_Fetch16, DisconnectRegFileHigh_Mov, or_37_out);
  or or_45 (DisconnectRegFileLow, or_37_out, DisconnectRegFileLow_Ldhl, DisconnectRegFileLow_Fetch16, DisconnectRegFileLow_Mov);
  nor nor_1 (RegLow2DbusE, RegLow2DbusE_ALU, RegLow2DbusE_Push, RegLow2DbusE_Mov, RegLow2DbusE_Lda, RegLow2DbusE_Ldax, RegLow2DbusE_Ldhl, DisconnectRegFile_Out, LowInrDcr, DisconnectRegFile_Daa);
  nor nor_2 (RegHigh2DbusE, RegHigh2DbusE_ALU, RegHigh2DbusE_Push, RegHigh2DbusE_Mov, RegHigh2DbusE_Ldhl, RegHigh2DbusE_Inr);
  Seven_Seg_Hex seven_seg_hex_13 (.d(undriven_12[7:4]), .dp(1'b0));
  // _74573 _74573_1: pin names not known; wires that end beside it: 1'b0, 1'b0, 1'b1
  Seven_Seg_Hex seven_seg_hex_14 (.d(undriven_13[7:4]), .dp(1'b0));
  nor nor_3 (RegA_E, SrcA, SrcA);
  nor nor_4 (RegB_E, SrcB, or_38_out);
  nor nor_5 (RegC_E, SrcC, or_38_out);
  nor nor_6 (RegD_E, SrcD, or_39_out);
  nor nor_7 (RegE_E, SrcE, or_39_out);
  nor nor_8 (RegH_E, SrcH, or_40_out);
  nor nor_9 (RegL_E, SrcL, or_40_out);
  nor nor_10 (RegW_E, or_41_out, or_41_out);
  nor nor_11 (RegZ_E, or_41_out, DisconnectRegFileLow_Fetch16);
  Seven_Seg_Hex seven_seg_hex_15 (.d(undriven_13[3:0]), .dp(1'b0));
  Seven_Seg_Hex seven_seg_hex_16 (.d(undriven_12[3:0]), .dp(1'b0));
  or or_46 (or_46_out, BCck_Lxi, BCck_Lxi);
  or or_47 (or_47_out, DEck_Lxi, DEck_Xchg);
  or or_48 (or_48_out, HLck_Lxi, HLck_Lxi);
  or or_49 (or_49_out, WZck_Xchg, WZck_Xchg);
  not not_10 (RegLow2DB_Dir, RegLow2DbusE);
  and and_83 (and_83_out, DisconnectRegFileLow, RegLow2DbusE);
  or or_50 (RegB_Ck, B_Ck, or_46_out);
  or or_51 (RegC_Ck, C_Ck, or_46_out);
  or or_52 (RegD_Ck, D_Ck, or_47_out);
  or or_53 (RegE_Ck, E_Ck, or_47_out);
  or or_54 (RegH_Ck, H_Ck, or_48_out);
  or or_55 (RegL_Ck, L_Ck, or_48_out);
  nor nor_12 (RegW_Ck, W_Ck, or_49_out);
  nor nor_13 (RegZ_Ck, Z_Ck, or_49_out);
  nor nor_14 (Regs2AbusE, DisconnectRegFile_Jmp, DisconnectRegFile_Mvi, DisconnectRegFile_Lxi, DisconnectRegFile_Rst, DisconnectRegFile_Ret, DisconnectRegFile_Call, DisconnectRegFile_SphlPchl, Regs2AbusE_Mov, Regs2AbusE_Lda, Regs2AbusE_Lhld, Regs2AbusE_Ldax, Regs2AbusE_Inx, DisconnectRegFile_Xthl, RegFileAddHL, HL_E_ALU);
  or or_56 (Regs2AbusLat, DisconnectRegFile_Jmp, DisconnectRegFile_Mvi, DisconnectRegFile_Lxi, DisconnectRegFile_Rst, DisconnectRegFile_Ret, DisconnectRegFile_Call, DisconnectRegFile_SphlPchl, Regs2AbusLat_Mov, HL_E_ALU, Regs2AbusLat_Lhld, Regs2AbusLat_Ldax, Regs2AbusLat_Inx, Regs2AbusLat_Xthl, Regs2AbusLat_Dad, Regs2AbusLat_Fetch16);
  or or_57 (ZW_plus_1, ZW_plus_1_LDHL, ZW_plus_1_Inx);
  nor nor_15 (IncLow2DbusE, IncLow2DbusE_Inx, IncLow2DbusE_Xthl, IncLow2DbusE_Dad);
  nor nor_16 (IncHigh2DbusE, IncHigh2DbusE_Inx, IncHigh2DbusE_Xthl, IncHigh2DbusE_Dad);
  not not_11 (not_11_out, Abus2Rbus_E);
  // _74245 _74245_2: pin names not known; wires that end beside it: 1'b1, RegLow2DB_Dir, and_83_out, 1'b0
  // _74574 _74574_6: pin names not known; wires that end beside it: 1'b1, 1'b0
  // _74574 _74574_7: pin names not known; wires that end beside it: 1'b1, 1'b0
  // _74574 _74574_8: pin names not known; wires that end beside it: 1'b1, 1'b0
  // _74574 _74574_9: pin names not known; wires that end beside it: 1'b1, 1'b0
  // _74574 _74574_10: pin names not known; wires that end beside it: 1'b1, 1'b0
  or or_58 (_16bitAddrLoad_Lda, OpLDA, OpSTA);
  and and_84 (Regs2AbusE_Lda, _16bitAddrLoad_Lda, T3);
  and and_85 (Finish_Lda, _16bitAddrLoad_Lda, P3);
  BusSplitter #(.Bits(8)) bussplitter_3 (.D(DataBus), .OE(not_12_out));  // open: D0, D1, D2, D3, D4, D5, D6, D7
  BusSplitter #(.Bits(8)) bussplitter_4 (.D(RegLowBus), .OE(RegLow2DB_Dir));  // open: D0, D1, D2, D3, D4, D5, D6, D7
  not not_12 (not_12_out, RegLow2DB_Dir);
  and and_86 (DBIN_Lda, OpLDA, Regs2AbusE_Lda);
  and and_87 (RegLow2DbusE_Lda, Regs2AbusE_Lda, OpSTA);
  and and_88 (DstA_LDA, OpLDA, Finish_Lda);
  and and_89 (MEMW_Lda, Finish_Lda, OpSTA);
  LED led_11 (.in(OpSTA));
  LED led_12 (.in(OpLDA));
  or or_59 (or_59_out, OpRAL, OpRLC);
  or or_60 (or_60_out, OpRAR, OpRRC);
  // _74541 _74541_11: pin names not known; wires that end beside it: RegA_Ck, 1'b0, 1'b1, RegA_E, RegA_E, 1'b0
  // _74541 _74541_12: pin names not known; wires that end beside it: RegC_Ck, 1'b0, 1'b1, RegC_E, RegC_E, 1'b0
  // _74541 _74541_13: pin names not known; wires that end beside it: RegE_Ck, 1'b0, 1'b1, RegE_E, RegE_E, 1'b0
  // _74541 _74541_14: pin names not known; wires that end beside it: RegL_Ck, 1'b0, 1'b1, RegL_E, RegL_E, 1'b0
  // _74541 _74541_15: pin names not known; wires that end beside it: RegZ_Ck, 1'b0, 1'b1, RegZ_E, RegZ_E, 1'b0
  LED led_13 (.in(or_59_out));
  and and_90 (and_90_out, or_59_out, T1);
  or or_61 (or_61_out, OpCMA, or_60_out, or_59_out);
  and and_91 (CarryCk_Rot, or_61_out, P1);
  LED led_14 (.in(or_60_out));
  and and_92 (and_92_out, or_60_out, T1);
  LED led_15 (.in(OpCMA));
  and and_93 (and_93_out, OpCMA, T1);
  not not_13 (not_13_out, DstIsMem);
  LED led_16 (.in(GrpMVI));
  and and_94 (MEMR_Mvi, GrpMVI, T1);
  and and_95 (DstE_MVI, GrpMVI, P1);
  and and_96 (DisconnectRegFile_Mvi, GrpMVI, DstIsMem, T2);
  and and_97 (MEMW_Mvi, GrpMVI, DstIsMem, P2);
  and and_98 (and_98_out, GrpMVI, P1, not_13_out);
  not not_14 (not_14_out, and_90_out);
  not not_15 (not_15_out, and_92_out);
  not not_16 (not_16_out, and_93_out);
  // _74541 _74541_16: pin names not known; wires that end beside it: 1'b0, not_11_out, not_11_out, 1'b1, RegLowBus
  or or_62 (DBIN_Mvi, MEMR_Mvi, MEMR_Mvi);
  or or_63 (Finish_Mvi, MEMW_Mvi, and_98_out);
  _74541 _74541_17 (
    .pin1(not_14_out), .pin2(AccBus[0]), .pin3(AccBus[1]), .pin4(AccBus[2]), .pin5(AccBus[3]),
    .pin6(AccBus[4]), .pin7(AccBus[5]), .pin8(AccBus[6]), .pin9(AccBus[7]), .pin10(1'b0),
    .pin11(_74541_17_pin11), .pin12(DataBus[7]), .pin13(DataBus[6]), .pin14(DataBus[5]), .pin15(DataBus[4]),
    .pin16(DataBus[3]), .pin17(DataBus[2]), .pin18(DataBus[1]), .pin19(not_14_out), .pin20(1'b1));
  _74541 _74541_18 (
    .pin1(not_15_out), .pin2(AccBus[0]), .pin3(AccBus[1]), .pin4(AccBus[2]), .pin5(AccBus[3]),
    .pin6(AccBus[4]), .pin7(AccBus[5]), .pin8(AccBus[6]), .pin9(AccBus[7]), .pin10(1'b0), .pin11(DataBus[6]),
    .pin12(DataBus[5]), .pin13(DataBus[4]), .pin14(DataBus[3]), .pin15(DataBus[2]), .pin16(DataBus[1]),
    .pin17(DataBus[0]), .pin18(_74541_18_pin18), .pin19(not_15_out), .pin20(1'b1));
  _74540 _74540_1 (
    .pin1(not_16_out), .pin2(AccBus[0]), .pin3(AccBus[1]), .pin4(AccBus[2]), .pin5(AccBus[3]),
    .pin6(AccBus[4]), .pin7(AccBus[5]), .pin8(AccBus[6]), .pin9(AccBus[7]), .pin10(1'b0), .pin11(DataBus[7]),
    .pin12(DataBus[6]), .pin13(DataBus[5]), .pin14(DataBus[4]), .pin15(DataBus[3]), .pin16(DataBus[2]),
    .pin17(DataBus[1]), .pin18(DataBus[0]), .pin19(not_16_out), .pin20(1'b1));
  Seven_Seg_Hex seven_seg_hex_17 (.d(AccBus[7:4]), .dp(1'b0));
  Seven_Seg_Hex seven_seg_hex_18 (.d(RegC[7:4]), .dp(1'b0));
  Seven_Seg_Hex seven_seg_hex_19 (.d(RegE[7:4]), .dp(1'b0));
  Seven_Seg_Hex seven_seg_hex_20 (.d(RegL[7:4]), .dp(1'b0));
  Seven_Seg_Hex seven_seg_hex_21 (.d(RegZ[7:4]), .dp(1'b0));
  _74157 _74157_1 (
    .pin1(DSTREG[1]), .pin2(_74541_18_pin18), .pin3(CarryFlag), .pin4(_74157_1_pin4), .pin5(1'b0),
    .pin6(1'b0), .pin8(1'b0), .pin10(1'b0), .pin11(1'b0), .pin12(_74157_1_pin12), .pin13(CarryFlag),
    .pin14(_74541_17_pin11), .pin15(1'b0), .pin16(1'b1));  // open: pin7, pin9
  Seven_Seg_Hex seven_seg_hex_22 (.d(RegLowBus[7:4]), .dp(1'b0));
  Seven_Seg_Hex seven_seg_hex_23 (.d(AccBus[3:0]), .dp(1'b0));
  Seven_Seg_Hex seven_seg_hex_24 (.d(RegC[3:0]), .dp(1'b0));
  Seven_Seg_Hex seven_seg_hex_25 (.d(RegE[3:0]), .dp(1'b0));
  Seven_Seg_Hex seven_seg_hex_26 (.d(RegL[3:0]), .dp(1'b0));
  Seven_Seg_Hex seven_seg_hex_27 (.d(RegZ[3:0]), .dp(1'b0));
  Seven_Seg_Hex seven_seg_hex_28 (.d(RegLowBus[3:0]), .dp(1'b0));
  assign DataBus[0] = ~not_14_out ? _74157_1_pin12 : 1'bz;  // DriverInvSel driverinvsel_1
  assign DataBus[7] = ~not_15_out ? _74157_1_pin4 : 1'bz;  // DriverInvSel driverinvsel_2
  or or_64 (or_64_out, Regs2AbusE, DisconnectRegFile_Xthl);
  and and_99 (and_99_out, and_90_out, _74541_17_pin11);
  and and_100 (and_100_out, _74541_18_pin18, and_92_out);
  or or_65 (or_65_out, OpRet, GrpCondRet);
  or or_66 (CarryData_Rot, and_99_out, and_100_out);
  Multiplexer #(.Selector_Bits(2), .Bits(8)) multiplexer_2 (
    .sel({RegFileAddHL, RegFileAdd00orFF}), .in_0({8{1'b0}}), .in_1({8{1'b1}}), .in_2(RegL), .in_3(RegL),
    .out({multiplexer_2_out_2, multiplexer_2_out}));
  LED led_17 (.in(or_65_out));
  and and_101 (and_101_out, or_65_out, T1);
  and and_102 (RegZck_Ret, or_65_out, P1);
  and and_103 (and_103_out, or_65_out, T2);
  and and_104 (RegWck_Ret, or_65_out, P2);
  and and_105 (DisconnectRegFile_Ret, or_65_out, T3);
  and and_106 (PcLoadCk_Ret1, or_65_out, P3);
  and and_107 (and_107_out, GrpCondRet, T1, nflagCondMet);
  or or_67 (DBIN_Ret, and_101_out, and_103_out);
  or or_68 (SpIncCk_Ret, and_103_out, DisconnectRegFile_Ret);
  or or_69 (Finish_Ret, PcLoadCk_Ret1, and_107_out);
  or or_70 (or_70_out, GrpInrDcr, OpDAA);
  // Probe on OpDAA
  not not_17 (not_17_out, GrpInrDcr);
  not not_18 (not_18_out, OpDAA);
  // _74283 _74283_3: pin names not known; wires that end beside it: Regs2AbusLat, ZW_plus_1, 1'b1, 1'b0, _74283_3_p5
  _74541 _74541_19 (
    .pin1(not_17_out), .pin2(1'b1), .pin3(GrpDcr), .pin4(GrpDcr), .pin5(GrpDcr), .pin6(GrpDcr),
    .pin7(GrpDcr), .pin8(GrpDcr), .pin9(GrpDcr), .pin10(1'b0), .pin11(_74541_19_pin11[7]),
    .pin12(_74541_19_pin11[6]), .pin13(_74541_19_pin11[5]), .pin14(_74541_19_pin11[4]),
    .pin15(_74541_19_pin11[3]), .pin16(_74541_19_pin11[2]), .pin17(_74541_19_pin11[1]),
    .pin18(_74541_19_pin11[0]), .pin19(not_17_out), .pin20(1'b1));
  // _74541 _74541_20: pin names not known; wires that end beside it: or_70_out, 1'b0, 1'b1, or_70_out
  _74541 _74541_21 (
    .pin1(not_18_out), .pin2(1'b0), .pin3(_74541_21_pin3), .pin4(_74541_21_pin3), .pin5(1'b0), .pin6(1'b0),
    .pin7(_74541_21_pin7), .pin8(_74541_21_pin7), .pin9(1'b0), .pin10(1'b0), .pin11(_74541_19_pin11[7]),
    .pin12(_74541_19_pin11[6]), .pin13(_74541_19_pin11[5]), .pin14(_74541_19_pin11[4]),
    .pin15(_74541_19_pin11[3]), .pin16(_74541_19_pin11[2]), .pin17(_74541_19_pin11[1]),
    .pin18(_74541_19_pin11[0]), .pin19(not_18_out), .pin20(1'b1));
  // _74541 _74541_22: pin names not known; wires that end beside it: 1'b0, or_64_out, or_64_out, 1'b1
  // _74541 _74541_23: pin names not known; wires that end beside it: 1'b0, IncLow2DbusE, IncLow2DbusE, 1'b1
  LED led_18 (.in(GrpPOP));
  and and_108 (FlgUpdateE_PopPsw, GrpPOP, T1);
  and and_109 (and_109_out, GrpPOP, P1);
  // And and_110 has open pins: In_1=GrpPOP, In_2=T2, out=open
  and and_111 (and_111_out, GrpPOP, P2);
  and and_112 (and_112_out, GrpPOP, T3);
  and and_113 (and_113_out, GrpPOP, P3);
  and and_114 (Finish_Pop, GrpPOP, P4);
  // _74283 _74283_4: pin names not known; wires that end beside it: _74283_3_p5, 1'b1, 1'b0, RegIncCarry
  or or_71 (SpInc_Pop, and_111_out, Finish_Pop);
  or or_72 (or_72_out, isArith, or_70_out);
  or or_73 (enableCarryIn, ADC, SBB);
  // _74573 _74573_2: pin names not known; wires that end beside it: 1'b0, 1'b0, 1'b1
  or or_74 (DBIN_Pop, FlgUpdateE_PopPsw, and_112_out);
  and and_115 (and_115_out, CarryFlag, enableCarryIn);
  // Probe on _74541_19_pin11
  // Probe on DataBus
  Seven_Seg_Hex seven_seg_hex_29 (.d(undriven_10[7:4]), .dp(1'b0));
  Seven_Seg_Hex seven_seg_hex_30 (.d(undriven_11[7:4]), .dp(1'b0));
  or or_75 (or_75_out, and_109_out, and_113_out);
  xor xor_1 (xor_1_out, isSubtraction, and_115_out);
  xor xor_2 (xor_9_out[0], DataBus[0], isSubtraction);
  xor xor_3 (xor_9_out[1], DataBus[1], isSubtraction);
  xor xor_4 (xor_9_out[2], DataBus[2], isSubtraction);
  xor xor_5 (xor_9_out[3], DataBus[3], isSubtraction);
  xor xor_6 (xor_9_out[4], DataBus[4], isSubtraction);
  xor xor_7 (xor_9_out[5], DataBus[5], isSubtraction);
  xor xor_8 (xor_9_out[6], DataBus[6], isSubtraction);
  xor xor_9 (xor_9_out[7], DataBus[7], isSubtraction);
  Seven_Seg_Hex seven_seg_hex_31 (.d(undriven_10[3:0]), .dp(1'b0));
  Seven_Seg_Hex seven_seg_hex_32 (.d(undriven_11[3:0]), .dp(1'b0));
  not not_19 (not_19_out, RP_SP);
  and and_116 (and_116_out, DataBus[1], DataBus[3]);
  and and_117 (and_117_out, DataBus[4], DataBus[7]);
  and and_118 (and_118_out, DataBus[2], DataBus[3]);
  and and_119 (and_119_out, DataBus[4], DataBus[7]);
  and and_120 (and_120_out, DataBus[5], DataBus[7]);
  and and_121 (and_121_out, DataBus[6], DataBus[7]);
  and and_122 (LowPOP, FlgUpdateE_PopPsw, not_19_out);
  and and_123 (DstE_POP, not_19_out, or_75_out);
  and and_124 (FlgUpdateCk_PopPsw, and_109_out, RP_SP);
  and and_125 (DstA_PopPsw, RP_SP, and_113_out);
  // _74283 _74283_5: pin names not known; wires that end beside it: xor_1_out, 1'b1, 1'b0, _74283_5_p4, 1'b0
  // _74283 _74283_6: pin names not known; wires that end beside it: _74283_5_p4, 1'b1, 1'b0, _74283_6_p4
  and and_126 (and_126_out, and_116_out, and_117_out);
  and and_127 (and_127_out, and_118_out, and_119_out);
  or or_76 (or_76_out, and_120_out, and_121_out);
  nor nor_17 (nor_17_out, SpDec_Inx, SpDec_Inx, DisconnectRegFile_Push, SpDec_Call, SpDec_Call, MemE_Rst, IncLow2DbusE_Xthl);
  nor nor_18 (nor_18_out, SpInc_Xthl, SpInc_Inx, SpInc_Pop, SpIncCk_Ret, SpIncCk_Ret);
  nor nor_19 (nor_19_out, SpLoadCk_Lxi, SpLoadCk_SphlPchl);
  nor nor_20 (nor_20_out, SpE_Xthl, DisconnectRegFile_Push, DBIN_Pop, DBIN_Ret, SpDec_Call, MemE_Rst, Abus2Rbus_E);
  not not_20 (not_20_out, or_72_out);
  // Probe on undriven_9
  or or_77 (or_77_out, and_126_out, and_127_out);
  // _74541 _74541_24: pin names not known; wires that end beside it: not_20_out, 1'b1, not_20_out
  or or_78 (_74541_21_pin3, and_118_out, AuxCarryFlag, and_116_out);
  or or_79 (_74541_21_pin7, or_77_out, CarryFlag, or_76_out);
  NegEdge negedge_1 (.i(nor_17_out), .o(negedge_1_o));
  NegEdge negedge_2 (.i(nor_18_out), .o(negedge_2_o));
  or or_80 (or_80_out, isSubtraction, GrpDcr);
  xor xor_10 (xor_10_out, _74283_6_p4, isSubtraction);
  not not_21 (not_21_out, negedge_1_o);
  not not_22 (not_22_out, negedge_2_o);
  xor xor_11 (xor_11_out, or_80_out, _74283_5_p4);
  and and_128 (and_128_out, AccBus[3], DataBus[3], ANA);
  and and_129 (and_129_out, isArith, xor_10_out);
  Reset #(.invertOutput("false")) reset_1 (.out(reset_1_out));
  or or_81 (or_81_out, LowPOP, LowPOP, IncLow2DbusE_Inx);
  and and_130 (and_130_out, not_23_out, DSTREG[0]);
  not not_23 (not_23_out, GrpInxDcx);
  or or_82 (or_82_out, Toff, ALUe_ALU, KillSrc_Mov, KillSrc_Mov);
  or or_83 (or_83_out, LowPUSH, LowInrDcr);
  or or_84 (or_84_out, Toff, ALUe_InrDcr);
  or or_85 (or_85_out, GrpPUSH, GrpInrDcr);
  LED led_19 (.in(GrpPUSH));
  and and_131 (and_131_out, GrpPUSH, T1);
  and and_132 (and_132_out, GrpPUSH, T2);
  and and_133 (and_133_out, GrpPUSH, P1);
  and and_134 (Finish_Push, GrpPUSH, P2);
  not not_24 (not_24_out, RP_SP);
  // Probe on AluResultBus
  nor nor_21 (nor_21_out, ANA, ORA, XRA);
  _74193 _74193_1 (
    .pin1(A1), .pin2(SP[1]), .pin3(SP[0]), .pin4(not_21_out), .pin5(not_22_out), .pin6(SP[2]), .pin7(SP[3]),
    .pin8(1'b0), .pin9(A3), .pin10(A2), .pin11(nor_19_out), .pin12(_74193_1_pin12), .pin13(_74193_1_pin13),
    .pin14(reset_1_out), .pin15(A0), .pin16(1'b1));
  // _74541 _74541_25: pin names not known; wires that end beside it: SP[3:0], SP[7:4], SP[11:8], SP[15:12], 1'b1, 1'b0, 1'b1, 1'b1
  nor nor_22 (nor_22_out, GrpMOV, _16bitAddrLoad_Lxi, GrpInxDcx, GrpMVI, GrpPOP, GrpInrDcr);
  or or_86 (or_86_out, DstE_MVI, DstE_InrDcr, DstE_InrDcr, DstE_InxDcx, DstE_MOV, DstE_POP);
  or or_87 (or_87_out, GrpALU, GrpMVI, GrpMOV);
  or or_88 (or_88_out, xor_11_out, and_128_out);
  or or_89 (or_89_out, or_81_out, and_130_out);
  and and_135 (ACo, nor_21_out, or_88_out);
  Multiplexer multiplexer_3 (.sel(OpDAA), .in_0(and_129_out), .in_1(_74541_21_pin7), .out(CYo));
  _74238 _74238_1 (
    .pin1(or_89_out), .pin2(DSTREG[1]), .pin3(DSTREG[2]), .pin4(nor_22_out), .pin5(1'b0), .pin6(or_86_out),
    .pin7(_74238_1_pin7), .pin8(1'b0), .pin9(DstM), .pin10(_74238_1_pin10), .pin11(_74238_1_pin11),
    .pin12(E_Ck), .pin13(D_Ck), .pin14(C_Ck), .pin15(B_Ck), .pin16(1'b1));
  _74238 _74238_2 (
    .pin1(IR[0]), .pin2(IR[1]), .pin3(IR[2]), .pin4(T0), .pin5(or_82_out), .pin6(or_87_out),
    .pin7(_74238_2_pin7), .pin8(1'b0), .pin9(_74238_2_pin9), .pin10(_74238_2_pin10), .pin11(_74238_2_pin11),
    .pin12(_74238_2_pin12), .pin13(_74238_2_pin13), .pin14(_74238_2_pin14), .pin15(_74238_2_pin15),
    .pin16(1'b1));
  _74238 _74238_3 (
    .pin1(or_83_out), .pin2(DSTREG[1]), .pin3(DSTREG[2]), .pin4(T0), .pin5(or_84_out), .pin6(or_85_out),
    .pin7(_74238_3_pin7), .pin8(1'b0), .pin9(_74238_3_pin9), .pin10(_74238_3_pin10), .pin11(_74238_3_pin11),
    .pin12(_74238_3_pin12), .pin13(_74238_3_pin13), .pin14(_74238_3_pin14), .pin15(_74238_3_pin15),
    .pin16(1'b1));
  _74238 _74238_4 (
    .pin1(DSTREG[0]), .pin2(DSTREG[1]), .pin3(DSTREG[2]), .pin4(1'b0), .pin5(1'b0), .pin6(1'b1),
    .pin7(_74238_4_pin7), .pin8(1'b0), .pin9(DstIsMem), .pin10(_74238_4_pin10), .pin11(_74238_4_pin11),
    .pin12(_74238_4_pin12), .pin13(_74238_4_pin13), .pin14(_74238_4_pin14), .pin15(_74238_4_pin15),
    .pin16(1'b1));
  or or_90 (DisconnectRegFile_Push, and_131_out, and_132_out);
  or or_91 (MEMW_Push, and_133_out, Finish_Push);
  and and_136 (RegHigh2DbusE_Push, and_131_out, not_24_out);
  and and_137 (LowPUSH, not_24_out, and_132_out);
  and and_138 (Flags2DB, and_132_out, RP_SP);
  and and_139 (SrcA_PushPsw, RP_SP, and_131_out);
  or or_92 (RegLow2DbusE_Push, LowPUSH, SrcA_PushPsw);
  // _74541 _74541_26: pin names not known; wires that end beside it: 1'b1, 1'b0, 1'b1, 1'b1
  _74193 _74193_2 (
    .pin1(A5), .pin2(SP[5]), .pin3(SP[4]), .pin4(_74193_1_pin13), .pin5(_74193_1_pin12), .pin6(SP[6]),
    .pin7(SP[7]), .pin8(1'b0), .pin9(A7), .pin10(A6), .pin11(nor_19_out), .pin12(_74193_2_pin12),
    .pin13(_74193_2_pin13), .pin14(reset_1_out), .pin15(A4), .pin16(1'b1));
  or or_93 (SrcB, _74238_2_pin15, _74238_3_pin15);
  or or_94 (SrcC, _74238_2_pin14, _74238_3_pin14);
  or or_95 (SrcD, _74238_2_pin13, _74238_3_pin13);
  or or_96 (SrcE, _74238_2_pin12, _74238_3_pin12);
  or or_97 (or_97_out, _74238_2_pin11, _74238_3_pin11);
  or or_98 (or_98_out, _74238_2_pin10, _74238_3_pin10);
  or or_99 (SrcM, _74238_2_pin9, _74238_3_pin9);
  or or_100 (or_100_out, _74238_2_pin7, _74238_3_pin7);
  or or_101 (RP_BC, _74238_4_pin15, _74238_4_pin14);
  or or_102 (RP_DE, _74238_4_pin13, _74238_4_pin12);
  or or_103 (RP_HL, _74238_4_pin11, _74238_4_pin10);
  or or_104 (RP_SP, DstIsMem, _74238_4_pin7);
  // _74541 _74541_27: pin names not known; wires that end beside it: nor_20_out, 1'b0, 1'b1, nor_20_out
  or or_105 (H_Ck, Finish_XCHG, DstH_LDHL, CarryCk_Dad, _74238_1_pin11, DstH_Xtld);
  or or_106 (L_Ck, _74238_1_pin10, DstL_LDHL, DstL_Dad, Finish_XCHG, DstL_Xtld);
  or or_107 (RegA_Ck, _74238_1_pin7, DstA_Ldax, RegAck_ALU, DstA_LDA, CarryCk_Rot, DstA_PopPsw, CarryCk_Daa, Ack_IO, Ack_IO);
  or or_108 (SrcH, RegHigh2DbusE_Ldhl, RegHigh2DbusE_Ldhl, or_97_out);
  or or_109 (SrcL, or_98_out, RegLow2DbusE_Ldhl, RegLow2DbusE_Ldhl);
  or or_110 (SrcA, or_100_out, DisconnectRegFile_Daa, RegLow2DbusE_Lda, RegLow2DbusE_Ldax, DisconnectRegFile_Out, SrcA_PushPsw, SrcA_PushPsw);
  not not_25 (not_25_out, XRA);
  xor xor_12 (xor_12_out, AccBus[0], DataBus[0]);
  xor xor_13 (xor_13_out, AccBus[1], DataBus[1]);
  xor xor_14 (xor_14_out, AccBus[2], DataBus[2]);
  xor xor_15 (xor_15_out, AccBus[3], DataBus[3]);
  xor xor_16 (xor_16_out, AccBus[4], DataBus[4]);
  xor xor_17 (xor_17_out, AccBus[5], DataBus[5]);
  xor xor_18 (xor_18_out, AccBus[6], DataBus[6]);
  xor xor_19 (xor_19_out, AccBus[7], DataBus[7]);
  not not_26 (not_26_out, ORA);
  or or_111 (or_111_out, AccBus[0], DataBus[0]);
  or or_112 (or_112_out, AccBus[1], DataBus[1]);
  or or_113 (or_113_out, AccBus[2], DataBus[2]);
  or or_114 (or_114_out, AccBus[3], DataBus[3]);
  or or_115 (or_115_out, AccBus[4], DataBus[4]);
  or or_116 (or_116_out, AccBus[5], DataBus[5]);
  or or_117 (or_117_out, AccBus[6], DataBus[6]);
  or or_118 (or_118_out, AccBus[7], DataBus[7]);
  not not_27 (not_27_out, ANA);
  and and_140 (and_140_out, AccBus[0], DataBus[0]);
  and and_141 (and_141_out, AccBus[1], DataBus[1]);
  and and_142 (and_142_out, AccBus[2], DataBus[2]);
  and and_143 (and_143_out, AccBus[3], DataBus[3]);
  and and_144 (and_144_out, AccBus[4], DataBus[4]);
  and and_145 (and_145_out, AccBus[5], DataBus[5]);
  and and_146 (and_146_out, AccBus[6], DataBus[6]);
  and and_147 (and_147_out, AccBus[7], DataBus[7]);
  _74541 _74541_28 (
    .pin1(not_25_out), .pin2(xor_12_out), .pin3(xor_13_out), .pin4(xor_14_out), .pin5(xor_15_out),
    .pin6(xor_16_out), .pin7(xor_17_out), .pin8(xor_18_out), .pin9(xor_19_out), .pin10(1'b0),
    .pin11(AluResultBus[7]), .pin12(AluResultBus[6]), .pin13(AluResultBus[5]), .pin14(AluResultBus[4]),
    .pin15(AluResultBus[3]), .pin16(AluResultBus[2]), .pin17(AluResultBus[1]), .pin18(AluResultBus[0]),
    .pin19(not_25_out), .pin20(1'b1));
  _74541 _74541_29 (
    .pin1(not_26_out), .pin2(or_111_out), .pin3(or_112_out), .pin4(or_113_out), .pin5(or_114_out),
    .pin6(or_115_out), .pin7(or_116_out), .pin8(or_117_out), .pin9(or_118_out), .pin10(1'b0),
    .pin11(AluResultBus[7]), .pin12(AluResultBus[6]), .pin13(AluResultBus[5]), .pin14(AluResultBus[4]),
    .pin15(AluResultBus[3]), .pin16(AluResultBus[2]), .pin17(AluResultBus[1]), .pin18(AluResultBus[0]),
    .pin19(not_26_out), .pin20(1'b1));
  _74541 _74541_30 (
    .pin1(not_27_out), .pin2(and_140_out), .pin3(and_141_out), .pin4(and_142_out), .pin5(and_143_out),
    .pin6(and_144_out), .pin7(and_145_out), .pin8(and_146_out), .pin9(and_147_out), .pin10(1'b0),
    .pin11(AluResultBus[7]), .pin12(AluResultBus[6]), .pin13(AluResultBus[5]), .pin14(AluResultBus[4]),
    .pin15(AluResultBus[3]), .pin16(AluResultBus[2]), .pin17(AluResultBus[1]), .pin18(AluResultBus[0]),
    .pin19(not_27_out), .pin20(1'b1));
  _74193 _74193_3 (
    .pin1(A9), .pin2(SP[9]), .pin3(SP[8]), .pin4(_74193_2_pin13), .pin5(_74193_2_pin12), .pin6(SP[10]),
    .pin7(SP[11]), .pin8(1'b0), .pin9(A11), .pin10(A10), .pin11(nor_19_out), .pin12(_74193_3_pin12),
    .pin13(_74193_3_pin13), .pin14(reset_1_out), .pin15(A8), .pin16(1'b1));
  LED led_20 (.in(_16bitAddrLoad_Lxi));
  and and_148 (DisconnectRegFile_Lxi, _16bitAddrLoad_Lxi, T3);
  and and_149 (BCck_Lxi, _16bitAddrLoad_Lxi, RP_BC, P3);
  and and_150 (DEck_Lxi, _16bitAddrLoad_Lxi, RP_DE, P3);
  and and_151 (HLck_Lxi, _16bitAddrLoad_Lxi, RP_HL, P3);
  and and_152 (SpLoadCk_Lxi, _16bitAddrLoad_Lxi, RP_SP, P3);
  and and_153 (Finish_Lxi, _16bitAddrLoad_Lxi, P3);
  // _74541 _74541_31: pin names not known; wires that end beside it: nor_20_out, 1'b0, 1'b1, nor_20_out
  Reset #(.invertOutput("false")) reset_2 (.out(reset_2_out));
  Comparator #(.Bits(16)) comparator_1 (.a(PC), .b(16'h55d));  // open: gt, eq, lt
  or or_119 (or_119_out, ALUe_ALU, ALUe_Daa, ALUe_InrDcr);
  Seven_Seg_Hex seven_seg_hex_33 (.d(SP[15:12]), .dp(1'b0));
  not not_28 (not_28_out, or_119_out);
  or or_120 (or_120_out, ALUck_InrDcr, ALUck_Daa, ALUck_ALU);
  xor xor_20 (xor_20_out, AluResultBus[0], AluResultBus[1]);
  xor xor_21 (xor_21_out, AluResultBus[2], AluResultBus[3]);
  xor xor_22 (xor_22_out, AluResultBus[4], AluResultBus[5]);
  xor xor_23 (xor_23_out, AluResultBus[6], AluResultBus[7]);
  _74193 _74193_4 (
    .pin1(A13), .pin2(SP[13]), .pin3(SP[12]), .pin4(_74193_3_pin13), .pin5(_74193_3_pin12), .pin6(SP[14]),
    .pin7(SP[15]), .pin8(1'b0), .pin9(A15), .pin10(A14), .pin11(nor_19_out), .pin14(reset_1_out),
    .pin15(A12), .pin16(1'b1));  // open: pin12, pin13
  Seven_Seg_Hex seven_seg_hex_34 (.d(SP[11:8]), .dp(1'b0));
  nor nor_23 (nor_23_out, reset_2_out, Finish_Inx, Finish_Inx, Finish_Jmp, Finish_Mvi, Finish_Nop, Finish_XCHG, Finish_Lxi, Finish_Mov, Finish_Push, Finish_Pop, Finish_Ldax, Finish_SphlPchl, Finish_Ret, CarryCk_Stc, Finish_Call, Finish_Rst, Finish_IO, Finish_Di, Finish_ALU, DstL_Dad, Finish_Lda, Finish_LDHL, Finish_Jmp, Finish_Xthl, DstE_InrDcr, Finish_Hlt, CarryCk_Rot, CarryCk_Daa);
  PullDown pulldown_3 (.out(pulldown_3_out));
  and and_154 (and_154_out, pulldown_3_out, T0);
  LED led_21 (.in(A10));
  LED led_22 (.in(D4));
  LED led_23 (.in(D5));
  LED led_24 (.in(D6));
  LED led_25 (.in(D7));
  LED led_26 (.in(D3));
  LED led_27 (.in(D2));
  LED led_28 (.in(D1));
  LED led_29 (.in(D0));
  LED led_30 (.in(RESET));
  LED led_31 (.in(HOLD));
  LED led_32 (.in(INT));
  LED led_33 (.in(Ph2));
  LED led_34 (.in(INTE));
  LED led_35 (.in(DBIN));
  LED led_36 (.in(nWR));
  LED led_37 (.in(SYNC));
  LED led_38 (.in(nWO));
  LED led_39 (.in(MEMR));
  LED led_40 (.in(OUT));
  LED led_41 (.in(INP));
  Reset reset_3 (.out(reset_3_out));
  assign driver_1_out = reset_3_out ? nMEMW : 1'bz;  // Driver driver_1
  nor nor_24 (nMEMW, MEMW_Lda, MEMW_Ldhl, MEMW_Call, MEMW_Push, MEMW_Mov, MEMW_Ldax, MEMW_Mvi, MEMW_Xthl, MEMW_Rst);
  not not_29 (nIOR, IOR_InOut);
  not not_30 (nIOW, IOW_InOut);
  // _74574 _74574_11: pin names not known; wires that end beside it: not_28_out, 1'b0, 1'b1, or_120_out
  nor nor_25 (nor_25_out, AluResultBus[0], AluResultBus[1]);
  nor nor_26 (nor_26_out, AluResultBus[2], AluResultBus[3]);
  nor nor_27 (nor_27_out, AluResultBus[4], AluResultBus[5]);
  nor nor_28 (nor_28_out, AluResultBus[6], AluResultBus[7]);
  or or_121 (or_121_out, and_154_out, OpHLT);
  // Probe on OpHLT
  PullDown pulldown_4 (.out(OpHLT));
  Button I (.out(I_out));
  PullUp pullup_1 (.out(nMEMR));
  PullUp pullup_2 (.out(nMEMW));
  PullUp pullup_3 (.out(nIOR));
  PullUp pullup_4 (.out(nIOW));
  PullUp pullup_5 (.out(nWR));
  PullUp pullup_6 (.out(driver_1_out));
  xor xor_24 (xor_24_out, xor_20_out, xor_21_out);
  xor xor_25 (xor_25_out, xor_22_out, xor_23_out);
  Seven_Seg_Hex seven_seg_hex_35 (.d(SP[7:4]), .dp(1'b0));
  _7474 _7474_1 (
    .pin1(_7474_1_pin1), .pin2(1'b0), .pin3(1'b0), .pin4(nor_23_out), .pin6(_7474_1_pin6), .pin7(1'b0),
    .pin10(1'b1), .pin11(1'b0), .pin12(1'b0), .pin13(1'b1), .pin14(1'b1));  // open: pin5, pin8, pin9
  not not_31 (_7474_1_pin1, T0);
  Button R (.out(R_out));
  not not_32 (not_32_out, I_out);
  and and_155 (and_155_out, not_32_out, I_out);
  not not_33 (not_33_out, T0);
  and and_156 (and_156_out, not_33_out, T0);
  LED led_42 (.in(A11));
  LED led_43 (.in(A12));
  LED led_44 (.in(A13));
  LED led_45 (.in(A14));
  LED led_46 (.in(A15));
  LED led_47 (.in(A9));
  LED led_48 (.in(A8));
  LED led_49 (.in(A7));
  LED led_50 (.in(A6));
  LED led_51 (.in(A5));
  LED led_52 (.in(A4));
  LED led_53 (.in(A3));
  LED led_54 (.in(A2));
  LED led_55 (.in(A1));
  LED led_56 (.in(A0));
  LED led_57 (.in(WAIT));
  LED led_58 (.in(READY));
  LED led_59 (.in(Ph1));
  LED led_60 (.in(HLDA));
  LED led_61 (.in(M1));
  LED led_62 (.in(INTA));
  LED led_63 (.in(HLTA));
  LED led_64 (.in(STACK));
  // Probe on {A15, A14, A13, A12, A11, A10, A9, A8, A7, A6, A5, A4, A3, A2, A1, A0}
  PullDown pulldown_5 (.out(pulldown_5_out));
  LED led_65 (.in(OpXcHG));
  and and_157 (DE_E_Xchg, OpXcHG, T1);
  and and_158 (WZck_Xchg, OpXcHG, P1);
  and and_159 (HL_E_Xchg, OpXcHG, T2);
  and and_160 (DEck_Xchg, OpXcHG, P2);
  and and_161 (WZ_E_Xchg, OpXcHG, T3);
  and and_162 (Finish_XCHG, OpXcHG, P3);
  and and_163 (and_163_out, nor_25_out, nor_26_out, nor_27_out, nor_28_out);
  xor xor_26 (xor_26_out, xor_24_out, xor_25_out);
  Seven_Seg_Hex seven_seg_hex_36 (.d(SP[3:0]), .dp(1'b0));
  not not_34 (not_34_out, R_out);
  and and_164 (and_164_out, not_34_out, R_out);
  not not_35 (not_35_out, or_121_out);
  and and_165 (and_165_out, not_35_out, or_121_out);
  RAMSinglePortSel #(.AddrBits(16), .isProgramMemory("true"), .Bits(8)) RAM1 (
    .A({A15, A14, A13, A12, A11, A10, A9, A8, A7, A6, A5, A4, A3, A2, A1, A0}), .CS(~pulldown_5_out),
    .WE(~driver_1_out), .OE(~nMEMR), .D(RAM1_d));
  or or_122 (_16bitAddrLoad_Jmp, OpJMP, GrpCondJmp);
  and and_166 (DisconnectRegFile_Jmp, _16bitAddrLoad_Jmp, T3);
  and and_167 (PcLoadCk_Jmp, _16bitAddrLoad_Jmp, P3);
  and and_168 (and_168_out, GrpCondJmp, P2, nflagCondMet);
  or or_123 (DisconnectRegFile_Xchg, DE_E_Xchg, HL_E_Xchg, WZ_E_Xchg);
  not not_36 (not_36_out, xor_26_out);
  RS_FF_AS rs_ff_as_1 (.S(and_155_out), .R(and_156_out), .Q(rs_ff_as_1_q));  // open: nQ
  PullDown pulldown_6 (.out(M1));
  PullDown pulldown_7 (.out(INTA));
  PullDown pulldown_8 (.out(HLTA));
  PullDown pulldown_9 (.out(STACK));
  PullDown pulldown_10 (.out(INP));
  PullDown pulldown_11 (.out(OUT));
  PullDown pulldown_12 (.out(MEMR));
  PullDown pulldown_13 (.out(nWO));
  PullDown pulldown_14 (.out(RESET));
  PullDown pulldown_15 (.out(Ph2));
  PullDown pulldown_16 (.out(Ph1));
  PullDown pulldown_17 (.out(HOLD));
  PullDown pulldown_18 (.out(HLDA));
  PullDown pulldown_19 (.out(DBIN));
  PullDown pulldown_20 (.out(WR));
  PullDown pulldown_21 (.out(SYNC));
  PullDown pulldown_22 (.out(WAIT));
  PullDown pulldown_23 (.out(READY));
  PullDown pulldown_24 (.out(INT));
  PullDown pulldown_25 (.out(INTE));
  not not_37 (not_37_out, DBIN);
  // Probe on RAM1_d
  not not_38 (not_38_out, nMEMR);
  LED led_66 (.in(_16bitAddrLoad_Jmp));
  or or_124 (Finish_Jmp, DisconnectRegFile_Jmp, and_168_out);
  _74574 _74574_12 (
    .pin1(not_28_out), .pin2(1'b0), .pin3(1'b0), .pin4(1'b0), .pin5(CYo), .pin6(ACo), .pin7(AluResultBus[7]),
    .pin8(and_163_out), .pin9(not_36_out), .pin10(1'b0), .pin11(or_120_out), .pin12(Po_ALU), .pin13(Zo_ALU),
    .pin14(So_ALU), .pin15(Ac_ALU), .pin16(Cy_ALU), .pin20(1'b1));  // open: pin17, pin18, pin19
  // Probe on and_164_out
  RS_FF_AS rs_ff_as_2 (.S(and_164_out), .R(and_165_out), .Q(rs_ff_as_2_q));  // open: nQ
  // Probe on and_165_out
  // Probe on rs_ff_as_1_q
  BusSplitter #(.Bits(8)) bussplitter_5 (
    .D(DataBus), .OE(not_37_out), .D0(D0), .D1(D1), .D2(D2), .D3(D3), .D4(D4), .D5(D5), .D6(D6), .D7(D7));
  BusSplitter #(.Bits(8)) bussplitter_6 (
    .D(RAM1_d), .OE(not_38_out), .D0(D0), .D1(D1), .D2(D2), .D3(D3), .D4(D4), .D5(D5), .D6(D6), .D7(D7));
  // Probe on RAM1_d
  or or_125 (DBIN, DBIN_Ret, DBIN_ALU, DBIN_FetchOp, DBIN_Fetch16, DBIN_InOut, DBIN_Mvi, DBIN_Pop, DBIN_Lda, DBIN_Mov, DBIN_Ldax, DBIN_Lhld, DBIN_Xthl, DBIN_InOut);
  nor nor_29 (nMEMR, DBIN_Ret, DBIN_ALU, DBIN_FetchOp, DBIN_Fetch16, MEMR_InOut, MEMR_Mvi, DBIN_Pop, DBIN_Lda, DBIN_Mov, DBIN_Ldax, DBIN_Lhld, DBIN_Xthl, DBIN_Xthl);
  or or_126 (or_126_out, rs_ff_as_2_q, rs_ff_as_1_q);
  nor nor_30 (nor_30_out, PcInc_FetchOp, PcInc_Fetch16, MEMR_Mvi, PcInc_ALU, MEMR_InOut);
  nor nor_31 (nor_31_out, PcDbHighE_Call, PcDbHighE_Rst);
  nor nor_32 (nor_32_out, PcDbLowE_Call, PcDbLowE_Rst);
  and and_169 (and_169_out, or_126_out, clk);
  ClkPulser clkpulser_1 (.CLK(clk), .Cnt(16'h3ea), .Trig(T_out), .Pulse(clkpulser_1_pulse));  // open: Finished
  Button T (.out(T_out));
  and and_170 (and_170_out, _74163_1_pin2, ~_74112_1_pin9);  // And
  and and_171 (and_171_out, ~_74163_1_pin2, _74112_1_pin9);  // And
  and and_172 (and_172_out, ~_74163_1_pin2, ~_74112_1_pin9);  // And
  PullDown pulldown_26 (.out(Po_ALU));
  PullDown pulldown_27 (.out(Zo_ALU));
  PullDown pulldown_28 (.out(So_ALU));
  PullDown pulldown_29 (.out(Ac_ALU));
  nor nor_33 (nor_33_out, PcLoadCk_Jmp, PcLoadCk_SphlPchl, PcLoadCk_Call1, PcLoadCk_Ret1, Finish_Rst);
  nor nor_34 (nor_34_out, DBIN_FetchOp, DBIN_Fetch16, MEMR_Mvi, MEMR_InOut, PcE_ALU);
  Button S (.out(S_out));
  LED led_67 (.in(and_170_out));
  LED led_68 (.in(and_171_out));
  LED led_69 (.in(and_172_out));
  LED led_70 (.in(T0));
  LED led_71 (.in(T1));
  LED led_72 (.in(P0));
  LED led_73 (.in(P1));
  // Probe on {IR[7:6], DSTREG, IR[2:0]}
  // Probe on {IR[7:6], DSTREG, IR[2:0]}
  // Probe on PC
  // Probe on {A15, A14, A13, A12, A11, A10, A9, A8, A7, A6, A5, A4, A3, A2, A1, A0}
  // Probe on DataBus
  // Probe on SP
  PullDown pulldown_30 (.out(Cy_ALU));
  or or_127 (TICK, S_out, and_169_out, clkpulser_1_pulse);
  LED led_74 (.in(T2));
  LED led_75 (.in(T3));
  LED led_76 (.in(P2));
  LED led_77 (.in(P3));
  LED led_78 (.in(OpLHLD));
  LED led_79 (.in(OpSHLD));
  or or_128 (_16bitAddrLoad_Lhld, OpLHLD, OpSHLD);
  or or_129 (or_129_out, T4, T5);
  and and_173 (DisconnectRegFileHigh_Ldhl, OpLHLD, T4);
  and and_174 (DisconnectRegFileLow_Ldhl, OpLHLD, T5);
  and and_175 (DstL_LDHL, OpLHLD, P4);
  and and_176 (DstH_LDHL, OpLHLD, P5);
  and and_177 (RegLow2DbusE_Ldhl, OpSHLD, T4);
  and and_178 (RegHigh2DbusE_Ldhl, OpSHLD, T5);
  and and_179 (and_179_out, OpSHLD, P4);
  and and_180 (and_180_out, OpSHLD, P5);
  Reset #(.invertOutput("false")) reset_4 (.out(reset_4_out));
  // Probe on TICK
  Reset reset_5 (.out(reset_5_out));
  LED led_80 (.in(T4));
  LED led_81 (.in(T5));
  LED led_82 (.in(P4));
  LED led_83 (.in(P5));
  // Probe on TICK
  and and_181 (DisconnectRegFile_Lhld, _16bitAddrLoad_Lhld, T3);
  and and_182 (Regs2AbusLat_Lhld, _16bitAddrLoad_Lhld, P3);
  // And and_183 has open pins: In_1=_16bitAddrLoad_Lhld, In_2=or_129_out, out=open
  and and_184 (ZW_plus_1_LDHL, _16bitAddrLoad_Lhld, T5);
  and and_185 (Finish_LDHL, _16bitAddrLoad_Lhld, P5);
  or or_130 (DBIN_Lhld, DisconnectRegFileHigh_Ldhl, DisconnectRegFileLow_Ldhl);
  or or_131 (MEMW_Ldhl, and_179_out, and_180_out);
  // Probe on AccBus
  // Probe on RegB
  // Probe on RegC
  // Probe on RegD
  // Probe on RegE
  // Probe on RegH
  // Probe on RegL
  // Probe on RegW
  // Probe on RegZ
  or or_132 (or_132_out, OpSPHL, OpPCHL);
  _74193 _74193_5 (
    .pin1(A1), .pin2(PC[1]), .pin3(PC[0]), .pin4(1'b1), .pin5(nor_30_out), .pin6(PC[2]), .pin7(PC[3]),
    .pin8(1'b0), .pin9(A3), .pin10(A2), .pin11(nor_33_out), .pin12(_74193_5_pin12), .pin13(_74193_5_pin13),
    .pin14(reset_4_out), .pin15(A0), .pin16(1'b1));
  // _74541 _74541_32: pin names not known; wires that end beside it: PC[3:0], PC[7:4], PC[11:8], PC[15:12], nor_32_out, 1'b0, 1'b1, nor_32_out
  _74163 _74163_1 (
    .pin1(_7474_1_pin6), .pin2(_74163_1_pin2), .pin3(1'b0), .pin4(1'b0), .pin5(1'b0), .pin6(1'b0),
    .pin7(1'b1), .pin8(1'b0), .pin9(1'b1), .pin10(1'b1), .pin12(_74163_1_pin12), .pin13(_74163_1_pin13),
    .pin14(_74163_1_pin14), .pin16(1'b1));  // open: pin11, pin15
  and and_186 (and_186_out, _74112_1_pin6, _74112_1_pin3, TICK);
  _74112 _74112_1 (
    .pin1(TICK), .pin2(1'b1), .pin3(_74112_1_pin3), .pin4(reset_5_out), .pin5(_74163_1_pin2),
    .pin6(_74112_1_pin6), .pin7(_74112_1_pin3), .pin8(1'b0), .pin9(_74112_1_pin9), .pin10(1'b1),
    .pin11(_74163_1_pin2), .pin12(_74112_1_pin6), .pin13(TICK), .pin14(reset_5_out), .pin15(1'b1),
    .pin16(1'b1));
  LED led_84 (.in(or_132_out));
  and and_187 (DisconnectRegFile_SphlPchl, or_132_out, T1);
  and and_188 (PcLoadCk_SphlPchl, or_132_out, OpPCHL, P1);
  and and_189 (SpLoadCk_SphlPchl, or_132_out, OpSPHL, P1);
  and and_190 (Finish_SphlPchl, or_132_out, P1);
  or or_133 (Regs2AbusE_Lhld, DBIN_Lhld, RegLow2DbusE_Ldhl, RegHigh2DbusE_Ldhl);
  or or_134 (or_134_out, FlgUpdateCk_PopPsw, DstE_InrDcr, Finish_ALU, CarryCk_Daa);
  or or_135 (or_135_out, CarryData_Dad, Cy_ALU, CarryData_Stc, CarryData_Rot, CarryData_Rot);
  or or_136 (or_136_out, Finish_ALU, FlgUpdateCk_PopPsw, CarryCk_Stc, CarryCk_Rot, CarryCk_Dad, CarryCk_Dad, CarryCk_Daa);
  not not_39 (not_39_out, and_186_out);
  not not_40 (Toff, not_39_out);
  // Probe on AccBus
  // Probe on {RegB, RegC}
  // Probe on {RegD, RegE}
  // Probe on {RegH, RegL}
  // Probe on SP
  // Probe PC on PC
  // _74541 _74541_33: pin names not known; wires that end beside it: nor_31_out, 1'b0, 1'b1, nor_31_out
  LED Zero (.in(ZeroFlag));
  LED AuxCarry (.in(AuxCarryFlag));
  LED Sign (.in(SignFlag));
  LED Parity (.in(ParityFlag));
  LED Carry (.in(CarryFlag));
  and and_191 (and_191_out, DataBus[7], FlgUpdateE_PopPsw);
  and and_192 (and_192_out, DataBus[6], FlgUpdateE_PopPsw);
  and and_193 (and_193_out, DataBus[4], FlgUpdateE_PopPsw);
  and and_194 (and_194_out, DataBus[2], FlgUpdateE_PopPsw);
  and and_195 (and_195_out, DataBus[0], FlgUpdateE_PopPsw);
  _74193 _74193_6 (
    .pin1(A5), .pin2(PC[5]), .pin3(PC[4]), .pin4(_74193_5_pin13), .pin5(_74193_5_pin12), .pin6(PC[6]),
    .pin7(PC[7]), .pin8(1'b0), .pin9(A7), .pin10(A6), .pin11(nor_33_out), .pin12(_74193_6_pin12),
    .pin13(_74193_6_pin13), .pin14(reset_4_out), .pin15(A4), .pin16(1'b1));
  _74238 _74238_5 (
    .pin1(_74163_1_pin14), .pin2(_74163_1_pin13), .pin3(_74163_1_pin12), .pin4(1'b0), .pin5(Toff),
    .pin6(1'b1), .pin8(1'b0), .pin10(T5), .pin11(T4), .pin12(T3), .pin13(T2), .pin14(T1), .pin15(T0),
    .pin16(1'b1));  // open: pin7, pin9
  _74238 _74238_6 (
    .pin1(_74163_1_pin14), .pin2(_74163_1_pin13), .pin3(_74163_1_pin12), .pin4(1'b0), .pin5(1'b0),
    .pin6(_74112_1_pin9), .pin8(1'b0), .pin10(P5), .pin11(P4), .pin12(P3), .pin13(P2), .pin14(P1),
    .pin15(P0), .pin16(1'b1));  // open: pin7, pin9
  Seven_Seg_Hex seven_seg_hex_37 (.d(PC[15:12]), .dp(1'b0));
  Seven_Seg_Hex seven_seg_hex_38 (.d({IR[7:6], DSTREG[2:1]}), .dp(1'b0));
  or or_137 (or_137_out, and_195_out, or_135_out);
  Seven_Seg_Hex seven_seg_hex_39 (.d(PC[11:8]), .dp(1'b0));
  Seven_Seg_Hex seven_seg_hex_40 (.d({DSTREG[0], IR[2:0]}), .dp(1'b0));
  LED led_85 (.in(GrpInrDcr));
  and and_196 (DisconnectRegFile_Inr, GrpInrDcr, T1);
  and and_197 (ALUck_InrDcr, GrpInrDcr, P1);
  and and_198 (ALUe_InrDcr, GrpInrDcr, T2);
  and and_199 (DstE_InrDcr, GrpInrDcr, P2);
  or or_138 (or_138_out, So_ALU, and_191_out);
  or or_139 (or_139_out, Zo_ALU, and_192_out);
  or or_140 (or_140_out, Ac_ALU, and_193_out);
  or or_141 (or_141_out, Po_ALU, and_194_out);
  and and_200 (P0x, T0, _74163_1_pin2);
  Seven_Seg_Hex seven_seg_hex_41 (.d(PC[7:4]), .dp(1'b0));
  // OpToTextStatic optotextstatic_1: pin names not known; wires that end beside it: {IR[7:6], DSTREG, IR[2:0]}
  _74574 _74574_13 (
    .pin1(1'b0), .pin2(or_138_out), .pin3(or_139_out), .pin4(1'b0), .pin5(or_140_out), .pin6(1'b0),
    .pin7(or_141_out), .pin8(1'b1), .pin9(1'b0), .pin10(1'b0), .pin11(or_134_out),
    .pin13(_74574_13_pin13[1]), .pin14(ParityFlag), .pin15(_74574_13_pin13[3]), .pin16(AuxCarryFlag),
    .pin17(_74574_13_pin13[5]), .pin18(ZeroFlag), .pin19(SignFlag), .pin20(1'b1));  // open: pin12
  not not_41 (not_41_out, Flags2DB);
  // _74541 _74541_34: pin names not known; wires that end beside it: nor_34_out, 1'b0, 1'b1, nor_34_out
  Seven_Seg_Hex seven_seg_hex_42 (.d(PC[3:0]), .dp(1'b0));
  and and_201 (RegHigh2DbusE_Inr, nIR3, DisconnectRegFile_Inr);
  and and_202 (LowInrDcr, DisconnectRegFile_Inr, DSTREG[0]);
  // Probe FLAGS on {SignFlag, ZeroFlag, _74574_13_pin13[5], AuxCarryFlag, _74574_13_pin13[3], ParityFlag, _74574_13_pin13[1], CarryFlag}
  SixteenSeg sixteenseg_1 (.led(undriven_5), .dp(1'b0));
  _74193 _74193_7 (
    .pin1(A9), .pin2(PC[9]), .pin3(PC[8]), .pin4(_74193_6_pin13), .pin5(_74193_6_pin12), .pin6(PC[10]),
    .pin7(PC[11]), .pin8(1'b0), .pin9(A11), .pin10(A10), .pin11(nor_33_out), .pin12(_74193_7_pin12),
    .pin13(_74193_7_pin13), .pin14(reset_4_out), .pin15(A8), .pin16(1'b1));
  Seven_Seg_Hex seven_seg_hex_43 (.d(DataBus[7:4]), .dp(1'b0));
  // _74541 _74541_35: pin names not known; wires that end beside it: nor_34_out, 1'b0, 1'b1, nor_34_out
  SixteenSeg sixteenseg_2 (.led(undriven_6), .dp(1'b0));
  and and_203 (IrLatch_FetchOp, delay_1_out, P0x);
  Delay #(.delayTime(5)) delay_1 (.in(P0x), .out(delay_1_out));
  not not_42 (not_42_out, delay_2_out);
  Delay #(.delayTime(5)) delay_2 (.in(P0), .out(delay_2_out));
  and and_204 (DisconnectRegFileHigh_Fetch16, or_142_out, T1);
  and and_205 (DisconnectRegFileLow_Fetch16, or_142_out, T2);
  and and_206 (RegZck_Fetch16, or_142_out, P1);
  and and_207 (Regs2AbusLat_Fetch16, or_142_out, P2);
  Seven_Seg_Hex seven_seg_hex_44 (.d(DataBus[3:0]), .dp(1'b0));
  SixteenSeg sixteenseg_3 (.led(undriven_7), .dp(1'b0));
  _74541 _74541_36 (
    .pin1(not_41_out), .pin2(CarryFlag), .pin3(_74574_13_pin13[1]), .pin4(ParityFlag),
    .pin5(_74574_13_pin13[3]), .pin6(AuxCarryFlag), .pin7(_74574_13_pin13[5]), .pin8(ZeroFlag),
    .pin9(SignFlag), .pin10(1'b0), .pin11(DataBus[7]), .pin12(DataBus[6]), .pin13(DataBus[5]),
    .pin14(DataBus[4]), .pin15(DataBus[3]), .pin16(DataBus[2]), .pin17(DataBus[1]), .pin18(DataBus[0]),
    .pin19(not_41_out), .pin20(1'b1));
  _7474 _7474_2 (
    .pin1(1'b1), .pin2(or_137_out), .pin3(or_136_out), .pin4(1'b1), .pin5(CarryFlag), .pin7(1'b0),
    .pin9(IntFlag), .pin10(SetInt), .pin11(1'b0), .pin12(1'b0), .pin13(ClrInt), .pin14(1'b1));  // open: pin6, pin8
  nor nor_35 (PcInc_FetchOp, not_42_out, P0);
  or or_142 (or_142_out, _16bitAddrLoad_Jmp, _16bitAddrLoad_Lda, _16bitAddrLoad_Lhld, _16bitAddrLoad_Lxi, _16bitAddrLoad_Call);
  or or_143 (or_143_out, RegZck_Fetch16, Regs2AbusLat_Fetch16);
  SixteenSeg sixteenseg_4 (.led(undriven_8), .dp(1'b0));
  _74153 _74153_1 (
    .pin1(1'b0), .pin2(DSTREG[2]), .pin3(SignFlag), .pin4(ParityFlag), .pin5(CarryFlag), .pin6(ZeroFlag),
    .pin7(_74153_1_pin7), .pin8(1'b0), .pin10(1'b0), .pin11(1'b0), .pin12(1'b0), .pin13(1'b0),
    .pin14(DSTREG[1]), .pin15(1'b0), .pin16(1'b1));  // open: pin9
  not not_43 (not_43_out, _74153_1_pin7);
  _74193 _74193_8 (
    .pin1(A13), .pin2(PC[13]), .pin3(PC[12]), .pin4(_74193_7_pin13), .pin5(_74193_7_pin12), .pin6(PC[14]),
    .pin7(PC[15]), .pin8(1'b0), .pin9(A15), .pin10(A14), .pin11(nor_33_out), .pin14(reset_4_out),
    .pin15(A12), .pin16(1'b1));  // open: pin12, pin13
  Seven_Seg_Hex seven_seg_hex_45 (.d(PC[15:12]), .dp(1'b0));
  Delay #(.delayTime(5)) delay_3 (.in(or_143_out), .out(delay_3_out));
  Seven_Seg_Hex seven_seg_hex_46 (.d({A15, A14, A13, A12}), .dp(1'b0));
  SixteenSeg sixteenseg_5 (.led(undriven), .dp(1'b0));
  xor xor_27 (flagCondMet, not_43_out, DSTREG[0]);
  LED IntEnabled (.in(IntFlag));
  Seven_Seg_Hex seven_seg_hex_47 (.d(PC[11:8]), .dp(1'b0));
  not not_44 (not_44_out, delay_3_out);
  Seven_Seg_Hex seven_seg_hex_48 (.d({A11, A10, A9, A8}), .dp(1'b0));
  Seven_Seg_Hex seven_seg_hex_49 (.d(PC[7:4]), .dp(1'b0));
  nor nor_36 (PcInc_Fetch16, not_44_out, or_143_out);
  SixteenSeg sixteenseg_6 (.led(undriven_2), .dp(1'b0));
  xor xor_28 (nflagCondMet, _74153_1_pin7, DSTREG[0]);
  PullDown pulldown_31 (.out(DBIN_FetchOp));
  or or_144 (DBIN_Fetch16, DisconnectRegFileHigh_Fetch16, T0, DisconnectRegFileLow_Fetch16);
  Seven_Seg_Hex seven_seg_hex_50 (.d({A7, A6, A5, A4}), .dp(1'b0));
  SixteenSeg sixteenseg_7 (.led(undriven_3), .dp(1'b0));
  Seven_Seg_Hex seven_seg_hex_51 (.d(PC[3:0]), .dp(1'b0));
  Seven_Seg_Hex seven_seg_hex_52 (.d({A3, A2, A1, A0}), .dp(1'b0));
  SixteenSeg sixteenseg_8 (.led(undriven_4), .dp(1'b0));
  or or_145 (or_145_out, enaALU_ALU, DisconnectRegFile_Inr);
  or or_146 (or_146_out, GrpALU, GrpImmOp);
  // Probe on DataBus
  or or_147 (or_147_out, GrpALU, GrpImmOp);
  _74573 _74573_3 (
    .pin1(1'b0), .pin2(DataBus[0]), .pin3(DataBus[1]), .pin4(DataBus[2]), .pin5(DataBus[3]),
    .pin6(DataBus[4]), .pin7(DataBus[5]), .pin8(DataBus[6]), .pin9(DataBus[7]), .pin10(1'b0),
    .pin11(IrLatch_FetchOp), .pin12(IR[7]), .pin13(IR[6]), .pin14(DSTREG[2]), .pin15(DSTREG[1]),
    .pin16(DSTREG[0]), .pin17(IR[2]), .pin18(IR[1]), .pin19(IR[0]), .pin20(1'b1));
  not not_45 (not_45_out, Db00E_Rst);
  not not_46 (not_46_out, DbIR345E_Rst);
  _74238 _74238_7 (
    .pin1(IR[6]), .pin2(IR[7]), .pin3(1'b0), .pin4(1'b0), .pin5(1'b0), .pin6(1'b1), .pin8(1'b0),
    .pin12(GrpBranchControl), .pin13(GrpALU), .pin14(GrpMOV), .pin15(GrpDatatransfer), .pin16(1'b1));  // open: pin7, pin9, pin10, pin11
  not not_47 (nIR0, IR[0]);
  not not_48 (nIR3, DSTREG[0]);
  LED led_86 (.in(OpDAA));
  and and_208 (DisconnectRegFile_Daa, OpDAA, T1);
  and and_209 (ALUck_Daa, OpDAA, P1);
  and and_210 (ALUe_Daa, OpDAA, T2);
  and and_211 (CarryCk_Daa, OpDAA, P2);
  and and_212 (DisconnectRegFile_ALU, GrpALU, T1);
  and and_213 (PcE_ALU, GrpImmOp, T1);
  and and_214 (PcInc_ALU, GrpImmOp, P1);
  LED led_87 (.in(or_147_out));
  and and_215 (and_215_out, or_147_out, T1);
  and and_216 (ALUck_ALU, or_147_out, P1);
  and and_217 (ALUe_ALU, or_147_out, T2);
  and and_218 (Finish_ALU, or_147_out, P2);
  not not_49 (not_49_out, or_145_out);
  _74541 _74541_37 (
    .pin1(not_45_out), .pin2(1'b0), .pin3(1'b0), .pin4(1'b0), .pin5(1'b0), .pin6(1'b0), .pin7(1'b0),
    .pin8(1'b0), .pin9(1'b0), .pin10(1'b0), .pin11(DataBus[7]), .pin12(DataBus[6]), .pin13(DataBus[5]),
    .pin14(DataBus[4]), .pin15(DataBus[3]), .pin16(DataBus[2]), .pin17(DataBus[1]), .pin18(DataBus[0]),
    .pin19(not_45_out), .pin20(1'b1));
  _74541 _74541_38 (
    .pin1(not_46_out), .pin2(1'b0), .pin3(1'b0), .pin4(1'b0), .pin5(DSTREG[0]), .pin6(DSTREG[1]),
    .pin7(DSTREG[2]), .pin8(1'b0), .pin9(1'b0), .pin10(1'b0), .pin11(DataBus[7]), .pin12(DataBus[6]),
    .pin13(DataBus[5]), .pin14(DataBus[4]), .pin15(DataBus[3]), .pin16(DataBus[2]), .pin17(DataBus[1]),
    .pin18(DataBus[0]), .pin19(not_46_out), .pin20(1'b1));
  and and_219 (_16bitAddrLoad_Lxi, nIR3, GrpLxiDad);
  and and_220 (OpDAD, GrpLxiDad, DSTREG[0]);
  and and_221 (GrpPUSH, nIR3, GrpStackPsh);
  and and_222 (GrpPOP, nIR3, GrpStackPop);
  or or_148 (GrpInrDcr, GrpInr, GrpDcr);
  _74238 _74238_8 (
    .pin1(DSTREG[0]), .pin2(DSTREG[1]), .pin3(DSTREG[2]), .pin4(not_49_out), .pin5(1'b0), .pin6(or_146_out),
    .pin7(CMP), .pin8(1'b0), .pin9(ORA), .pin10(XRA), .pin11(ANA), .pin12(SBB), .pin13(SUB), .pin14(ADC),
    .pin15(ADD), .pin16(1'b1));
  _74238 _74238_9 (
    .pin1(IR[0]), .pin2(IR[1]), .pin3(IR[2]), .pin4(1'b0), .pin5(1'b0), .pin6(GrpDatatransfer),
    .pin7(GrpRotFlag), .pin8(1'b0), .pin9(GrpMVI), .pin10(GrpDcr), .pin11(GrpInr), .pin12(GrpInxDcx),
    .pin13(GrpLoadStore), .pin14(GrpLxiDad), .pin15(OpNOP), .pin16(1'b1));
  _74238 _74238_10 (
    .pin1(IR[0]), .pin2(IR[1]), .pin3(IR[2]), .pin4(1'b0), .pin5(1'b0), .pin6(GrpBranchControl),
    .pin7(GrpRST), .pin8(1'b0), .pin9(GrpImmOp), .pin10(GrpStackPsh), .pin11(GrpCondCall),
    .pin12(GrpJmpOthers), .pin13(GrpCondJmp), .pin14(GrpStackPop), .pin15(GrpCondRet), .pin16(1'b1));
  not not_50 (not_50_out, SrcM);
  and and_223 (and_223_out, not_50_out, DisconnectRegFile_ALU);
  and and_224 (HL_E_ALU, DisconnectRegFile_ALU, SrcM);
  // Probe IR on {IR[7:6], DSTREG, IR[2:0]}
  Seven_Seg_Hex seven_seg_hex_53 (.d({IR[7:6], DSTREG[2:1]}), .dp(1'b0));
  Seven_Seg_Hex seven_seg_hex_54 (.d({DSTREG[0], IR[2:0]}), .dp(1'b0));
  not not_51 (not_51_out, DisconnectRegFile_Mvi);
  not not_52 (not_52_out, DstE_MVI);
  // _74574 _74574_14: pin names not known; wires that end beside it: not_51_out, 1'b0, 1'b1, not_52_out
  and and_225 (RegLow2DbusE_ALU, IR[0], and_223_out);
  and and_226 (RegHigh2DbusE_ALU, and_223_out, nIR0);
  LED led_88 (.in(OpSTC));
  LED led_89 (.in(OpCMC));
  or or_149 (or_149_out, OpCMC, OpSTC);
  not not_53 (not_53_out, CarryFlag);
  not not_54 (not_54_out, CMP);
  and and_227 (and_227_out, not_53_out, or_149_out, T1);
  and and_228 (CarryCk_Stc, or_149_out, P1);
  or or_150 (DBIN_ALU, HL_E_ALU, PcE_ALU);
  or or_151 (enaALU_ALU, and_215_out, ALUe_ALU);
  and and_229 (RegAck_ALU, Finish_ALU, not_54_out);
  or or_152 (isArith, ADD, ADC, CMP, SUB, SBB);
  or or_153 (isSubtraction, CMP, SBB, SUB);
  not not_55 (not_55_out, HoldDB2AB_E);
  not not_56 (not_56_out, HoldDB2AB_Ck);
  _74238 _74238_11 (
    .pin1(DSTREG[0]), .pin2(DSTREG[1]), .pin3(DSTREG[2]), .pin4(1'b0), .pin5(1'b0), .pin6(GrpLoadStore),
    .pin7(OpLDA), .pin8(1'b0), .pin9(OpSTA), .pin10(OpLHLD), .pin11(OpSHLD), .pin12(OpLdaxDE),
    .pin13(OpStaxDE), .pin14(OpLdaxBC), .pin15(OpStaxBC), .pin16(1'b1));
  _74238 _74238_12 (
    .pin1(DSTREG[0]), .pin2(DSTREG[1]), .pin3(DSTREG[2]), .pin4(1'b0), .pin5(1'b0), .pin6(GrpRotFlag),
    .pin7(OpCMC), .pin8(1'b0), .pin9(OpSTC), .pin10(OpCMA), .pin11(OpDAA), .pin12(OpRAR), .pin13(OpRAL),
    .pin14(OpRRC), .pin15(OpRLC), .pin16(1'b1));
  _74238 _74238_13 (
    .pin1(DSTREG[0]), .pin2(DSTREG[1]), .pin3(DSTREG[2]), .pin4(1'b0), .pin5(1'b0), .pin6(GrpStackPop),
    .pin7(OpSPHL), .pin8(1'b0), .pin10(OpPCHL), .pin14(OpRet), .pin16(1'b1));  // open: pin9, pin11, pin12, pin13, pin15
  _74238 _74238_14 (
    .pin1(DSTREG[0]), .pin2(DSTREG[1]), .pin3(DSTREG[2]), .pin4(1'b0), .pin5(1'b0), .pin6(GrpJmpOthers),
    .pin7(OpEi), .pin8(1'b0), .pin9(OpDi), .pin10(OpXcHG), .pin11(OpXtHL), .pin12(OpIn), .pin13(OpOut),
    .pin14(_74238_14_pin14), .pin15(OpJMP), .pin16(1'b1));
  _74238 _74238_15 (
    .pin1(DSTREG[0]), .pin2(DSTREG[1]), .pin3(DSTREG[2]), .pin4(1'b0), .pin5(1'b0), .pin6(GrpStackPsh),
    .pin8(1'b0), .pin14(OpCall), .pin16(1'b1));  // open: pin7, pin9, pin10, pin11, pin12, pin13, pin15
  or or_154 (CarryData_Stc, OpSTC, and_227_out);
  // _74574 _74574_15: pin names not known; wires that end beside it: not_55_out, 1'b0, 1'b1, not_56_out
  _74541 _74541_39 (
    .pin1(not_55_out), .pin2(1'b0), .pin3(1'b0), .pin4(1'b0), .pin5(1'b0), .pin6(1'b0), .pin7(1'b0),
    .pin8(1'b0), .pin9(1'b0), .pin10(1'b0), .pin11(A15), .pin12(A14), .pin13(A13), .pin14(A12), .pin15(A11),
    .pin16(A10), .pin17(A9), .pin18(A8), .pin19(not_55_out), .pin20(1'b1));
  or or_155 (or_155_out, OpOut, OpIn);
  and and_230 (DisconnectRegFile_Out, OpOut, T2);
  and and_231 (IOR_InOut, OpIn, T2);
  and and_232 (IOW_InOut, OpOut, P2);
  and and_233 (Ack_IO, OpIn, P2);
  and and_234 (MEMR_InOut, or_155_out, T1);
  and and_235 (HoldDB2AB_Ck, or_155_out, P1);
  LED OpIn_2 (.in(OpIn));
  LED OpOut_2 (.in(OpOut));
  or or_156 (DBIN_InOut, MEMR_InOut, IOR_InOut);
  or or_157 (HoldDB2AB_E, DisconnectRegFile_Out, IOR_InOut);
  or or_158 (Finish_IO, IOW_InOut, Ack_IO);

  // Other names for the same wires on the sheet: AddrBus[15:0] = {A15, A14, A13, A12, A11, A10, A9, A8, A7, A6, A5, A4, A3, A2, A1, A0};
  //   AddrBus_L[7:0] = {A7, A6, A5, A4, A3, A2, A1, A0}; AddrBus_H[7:0] = {A15, A14, A13, A12, A11, A10, A9, A8};
  //   DstH_Dad = CarryCk_Dad; enaALU_InrDcr = DisconnectRegFile_Inr; Finish_Dad = DstL_Dad; DstA_Rot = CarryCk_Rot;
  //   Finish_Rot = CarryCk_Rot; Finish_Stc = CarryCk_Stc; FlgUpdate_ALU = Finish_ALU; DstA_Daa = CarryCk_Daa;
  //   Finish_Daa = CarryCk_Daa; FlgUpdate_Daa = CarryCk_Daa; Finish_InrDcr = DstE_InrDcr;
  //   FlgUpdate_InrDcr = DstE_InrDcr; GrpLXI = _16bitAddrLoad_Lxi; HLck_Xchg = Finish_XCHG; HoldDB_Ck = DstE_MVI;
  //   SRCREG[2:0] = IR[2:0]; IR[5:3] = DSTREG; IR3 = DSTREG[0]; IR4 = DSTREG[1]; IR5 = DSTREG[2];
  //   KillSrc_ALU = ALUe_ALU; LowINX = IncLow2DbusE_Inx; MEMR_ALU = DBIN_ALU; MEMR_Lda = DBIN_Lda;
  //   MEMR_Ldax = DBIN_Ldax; MEMR_Lhld = DBIN_Lhld; MEMR_Mov = DBIN_Mov; MEMR_Xthl = DBIN_Xthl;
  //   MEMR_Fetch16 = DBIN_Fetch16; PcE_Fetch16 = DBIN_Fetch16; MEMR_FetchOp = DBIN_FetchOp;
  //   PcE_FetchOp = DBIN_FetchOp; PcE_IO = MEMR_InOut; PcInc_IO = MEMR_InOut; PcE_Mvi = MEMR_Mvi;
  //   PcInc_Mvi = MEMR_Mvi; PcLoadCk_Rst = Finish_Rst; RegHigh2DB_E = DisconnectRegFileHigh;
  //   RegLow2DB_E = DisconnectRegFileLow; RegLow2DbusE_Inr = LowInrDcr; Regs2AbusE_Dad = RegFileAddHL;
  //   Regs2AbusE_Xthl = DisconnectRegFile_Xthl; Regs2AbusE_ALU = HL_E_ALU; Regs2AbusLat_ALU = HL_E_ALU;
  //   RegWck_Fetch16 = Regs2AbusLat_Fetch16; HL_E_MVI = DisconnectRegFile_Mvi; HoldDB_E = DisconnectRegFile_Mvi;
  //   Regs2AbusE_Mvi = DisconnectRegFile_Mvi; Regs2AbusLat_Mvi = DisconnectRegFile_Mvi;
  //   HL_E_SPHL_PCHL = DisconnectRegFile_SphlPchl; Regs2AbusE_SphlPchl = DisconnectRegFile_SphlPchl;
  //   Regs2AbusLat_SphlPchl = DisconnectRegFile_SphlPchl; SpDec_Xthl = IncLow2DbusE_Xthl; SpE_Call = SpDec_Call;
  //   SpE_Dad = Abus2Rbus_E; MEMR_Pop = DBIN_Pop; SpE_Pop = DBIN_Pop; SpDec_Push = DisconnectRegFile_Push;
  //   SpE_Push = DisconnectRegFile_Push; MEMR_Ret = DBIN_Ret; SpE_Ret = DBIN_Ret; SpDec_Rst = MemE_Rst;
  //   SpE_Rst = MemE_Rst; RegLow2DbusE_Daa = DisconnectRegFile_Daa; SrcA_Daa = DisconnectRegFile_Daa;
  //   SrcA_LDA = RegLow2DbusE_Lda; SrcA_Ldax = RegLow2DbusE_Ldax; RegLow2DbusE_Out = DisconnectRegFile_Out;
  //   SrcA_Out = DisconnectRegFile_Out; SrcH_LDHL = RegHigh2DbusE_Ldhl; SrcL_LDHL = RegLow2DbusE_Ldhl;
  //   ToffIndDcr = ALUe_InrDcr; Regs2AbusE_Call = DisconnectRegFile_Call; Regs2AbusLat_Call = DisconnectRegFile_Call;
  //   WZ_E_Call = DisconnectRegFile_Call; Regs2AbusE_JMP = DisconnectRegFile_Jmp;
  //   Regs2AbusLat_JMP = DisconnectRegFile_Jmp; WZ_E_Jmp = DisconnectRegFile_Jmp; WZ_E_Lhld = DisconnectRegFile_Lhld;
  //   Regs2AbusE_Lxi = DisconnectRegFile_Lxi; Regs2AbusLat_Lxi = DisconnectRegFile_Lxi;
  //   WZ_E_Lxi = DisconnectRegFile_Lxi; Regs2AbusE_Ret = DisconnectRegFile_Ret;
  //   Regs2AbusLat_Ret = DisconnectRegFile_Ret; WZ_E_Ret = DisconnectRegFile_Ret;
  //   Regs2AbusE_Rst = DisconnectRegFile_Rst; Regs2AbusLat_Rst = DisconnectRegFile_Rst;
  //   WZ_E_Rst = DisconnectRegFile_Rst; Z_E_Fetch16 = DisconnectRegFileLow_Fetch16

  // Notes on the sheet:
  //   clk: Hz: 2147483647
  //   XTHL
  //   LDAX / STAX
  //   NOP / HLT
  //   -
  //   EI / DI
  //   AccBus
  //   DataBus
  //   AddrBus
  //   INX / DCX
  //   REGISTER FILE - HIGH - PART1
  //   DIR=1 A(in) B(out)
  //   MEMORY
  //   DAD
  //   MOV
  //   B
  //   D
  //   H
  //   W
  //   CALL
  //   HighBus
  //   REGISTER FILE - HIGH - PART2
  //   RST
  //   https://en.wikipedia.org/wiki/Intel_8080#Instruction_set
  //   https://github.com/begoon/8080ex1
  //   https://github.com/begoon/i8080-core
  //   https://www.pastraiser.com/cpu/i8080/i8080_opcodes.html?utm_source=chatgpt.com
  //   https://eliben.org/js8080/
  //   https://web.archive.org/web/20180224032116/http://emulator101.com/
  //   https://altairclone.com/downloads/cpu_tests/8080_8085%20CPU%20Exerciser.pdf
  //   https://grantmestrength.github.io/RetroComputerInstructionManual/intel8080.html
  //   LDA / STA
  //   REGISTER FILE - LOW - PART1
  //   ACC ROTATES / COMPLEMENT
  //   MVI
  //   A
  //   C
  //   E
  //   L
  //   Z
  //   RAR : A7 A6 A5 A4 A3 A2 A1 A0 → CY → A7
  //   LowBus
  //   RET
  //   REGISTER FILE - LOW - PART2
  //   ALU ARITHMETIC OPS
  //   POP
  //   CarryIn
  //   AuxCarryOut
  //   CarryOut
  //   Stack Pointer
  //   DEST / SOURCE DECODERS
  //   PUSH
  //   ALU LOGIC OPS
  //   LXI
  //   T-STATE & RUN CONTROL
  //   SP
  //   XCHG
  //   DE->WZ
  //   HL->DE
  //   WZ->HL
  //   JMP/ JPx
  //   CPU PINS
  //   * * * * * * * * * * * * * *
  //   LHLD / SHLD
  //   Program Counter
  //   SPHL / PCHL
  //   FLAGS
  //   Ac
  //   S
  //   P
  //   INR / DCR
  //   IR
  //   PC
  //   Flag conditional selector
  //   Fetch Opcode
  //   Fetch 16 bit address
  //   DBus
  //   ABus
  //   ALU instructions
  //   IR - Instruction reg
  //   DAA
  //   BUS CONSTANTS
  //   DbZero
  //   DbIR345
  //   00xx xxxx
  //   01xx xxxx
  //   10xx xxxx
  //   11xx xxxx
  //   00xx x000
  //   00xx x001
  //   00xx x010
  //   00xx x011
  //   00xx x100
  //   00xx x101
  //   00xx x110
  //   00xx x111
  //   11xx x000
  //   11xx x001
  //   11xx x010
  //   11xx x011
  //   11xx x100
  //   11xx x101
  //   11xx x110
  //   11xx x111
  //   STC/CMC
  //   OperandHold
  //   0000 0010
  //   0000 1010
  //   0001 0010
  //   0001 1010
  //   0010 0010
  //   0010 1010
  //   0011 0010
  //   0011 1010
  //   0000 0111
  //   0000 1111
  //   0001 0111
  //   0001 1111
  //   0010 0111
  //   0010 1111
  //   0011 0111
  //   0011 1111
  //   1100 1001
  //   1110 1001
  //   1111 1001
  //   1100 0011
  //   1100 1011
  //   1101 0011
  //   1101 1011
  //   1110 0011
  //   1110 1011
  //   1111 0011
  //   1111 1011
  //   1100 1101
  //   HoldDBtoAddrLow
  //   OUT / IN
endmodule
